// Logisim project question4.circ as structural Verilog: 1 circuit, main circuit main
module main (
  input  A,
  input  B,
  input  C,
  output Output
);

  wire A___B_____C___B_out, A___B_out, A___nB_out, C___B_out, n__A___B_____C___B_out, n_A___nB____C_out,
       n_A___nB_out, nB_out;

  and A___B (A___B_out, A, B);
  not nB (nB_out, B);
  and C___B (C___B_out, B, C);
  or A___nB (A___nB_out, A, nB_out);
  not n_A___nB (n_A___nB_out, A___nB_out);
  and n_A___nB____C (n_A___nB____C_out, n_A___nB_out, C);
  or A___B_____C___B (A___B_____C___B_out, A___B_out, C___B_out);
  or or_1 (Output, n_A___nB____C_out, n__A___B_____C___B_out);
  not n__A___B_____C___B (n__A___B_____C___B_out, A___B_____C___B_out);
endmodule
