// Logisim project question5.circ as structural Verilog: 1 circuit, main circuit main
module main (
  input  A,
  input  B,
  input  C,
  output Output_2,
  output Output_1
);

  wire A___B___C_out, A___B___nC_out, A___nB___nC_out, A___nB_out, nA___B_out, nA___nC_out, nA_out, nB_out,
       nC_out;

  not nA (nA_out, A);
  not nB (nB_out, B);
  not nC (nC_out, C);
  and nA___B (nA___B_out, nA_out, B);
  and A___nB (A___nB_out, A, nB_out);
  and A___B___nC (A___B___nC_out, A, B, nC_out);
  or or_1 (Output_1, nA___B_out, A___nB_out, A___B___nC_out);
  and nA___nC (nA___nC_out, nA_out, nC_out);
  and A___B___C (A___B___C_out, C, A, B);
  and A___nB___nC (A___nB___nC_out, A, nB_out, nC_out);
  or or_2 (Output_2, A___B___C_out, nA___nC_out, A___nB___nC_out);
endmodule
