// Logisim project question6.circ as structural Verilog: 1 circuit, main circuit main
module main (
  input  In1,
  input  In2,
  output Output
);

  wire clock_out, Not_In1, Not_In2, Not_Q0, Not_Q1, or_1_out, or_2_out, prodA, prodB, prodC, prodD, prodE,
       prodF, prodG, prodH, Q0, Q1;

  Clock clock (.out(clock_out));
  not not_1 (Not_In1, In1);
  not not_2 (Not_In2, In2);
  and and_1 (prodA, Q0, Not_In1, In2);
  and and_2 (prodB, Q0, In1, Not_In2);
  and and_3 (prodC, Not_Q0, Q1, Not_In1, In2);
  and and_4 (prodD, Not_Q0, Q1, In1, Not_In2);
  and and_5 (prodE, Not_Q0, Not_In1, In2);
  and and_6 (prodF, Not_Q0, In1, Not_In2);
  and and_7 (prodG, Q0, Q1, Not_In1, In2);
  and and_8 (prodH, Q0, Q1, In1, Not_In2);
  or or_1 (or_1_out, prodA, prodB, prodC, prodD);
  or or_2 (or_2_out, prodE, prodF, prodG, prodH);
  and and_9 (Output, Q1, Q0);
  D_Flip_Flop FF1 (.clk(clock_out), .D(or_1_out), .Q(Q1), .Qn(Not_Q1));  // open: preset, en, reset
  D_Flip_Flop FF0 (.clk(clock_out), .D(or_2_out), .Q(Q0), .Qn(Not_Q0));  // open: preset, en, reset
endmodule
