// Logisim project question7.circ as structural Verilog: 4 circuits, main circuit Adder 16 bit
module Adder_16_bit (
  input  [15:0] a,
  input  Cin,
  input  [15:0] b,
  output [15:0] Sum,
  output Cout
);

  wire bit_0_cout, bit_1_cout, bit_2_cout, bit_3_cout, bit_4_cout, bit_5_cout, bit_6_cout, bit_7_cout,
       bit_8_cout, bit_9_cout, bit_10_cout, bit_11_cout, bit_12_cout, bit_13_cout, bit_14_cout;

  Adder_1_bit bit_0 (.a(a[0]), .b(b[0]), .Cin(Cin), .Cout(bit_0_cout), .Sum(Sum[0]));
  Adder_1_bit bit_8 (.a(a[8]), .b(b[8]), .Cin(bit_7_cout), .Cout(bit_8_cout), .Sum(Sum[8]));
  Adder_1_bit bit_1 (.a(a[1]), .b(b[1]), .Cin(bit_0_cout), .Cout(bit_1_cout), .Sum(Sum[1]));
  Adder_1_bit bit_9 (.a(a[9]), .b(b[9]), .Cin(bit_8_cout), .Cout(bit_9_cout), .Sum(Sum[9]));
  Adder_1_bit bit_2 (.a(a[2]), .b(b[2]), .Cin(bit_1_cout), .Cout(bit_2_cout), .Sum(Sum[2]));
  Adder_1_bit bit_10 (.a(a[10]), .b(b[10]), .Cin(bit_9_cout), .Cout(bit_10_cout), .Sum(Sum[10]));
  Adder_1_bit bit_3 (.a(a[3]), .b(b[3]), .Cin(bit_2_cout), .Cout(bit_3_cout), .Sum(Sum[3]));
  Adder_1_bit bit_11 (.a(a[11]), .b(b[11]), .Cin(bit_10_cout), .Cout(bit_11_cout), .Sum(Sum[11]));
  Adder_1_bit bit_4 (.a(a[4]), .b(b[4]), .Cin(bit_3_cout), .Cout(bit_4_cout), .Sum(Sum[4]));
  Adder_1_bit bit_12 (.a(a[12]), .b(b[12]), .Cin(bit_11_cout), .Cout(bit_12_cout), .Sum(Sum[12]));
  Adder_1_bit bit_5 (.a(a[5]), .b(b[5]), .Cin(bit_4_cout), .Cout(bit_5_cout), .Sum(Sum[5]));
  Adder_1_bit bit_13 (.a(a[13]), .b(b[13]), .Cin(bit_12_cout), .Cout(bit_13_cout), .Sum(Sum[13]));
  Adder_1_bit bit_6 (.a(a[6]), .b(b[6]), .Cin(bit_5_cout), .Cout(bit_6_cout), .Sum(Sum[6]));
  Adder_1_bit bit_14 (.a(a[14]), .b(b[14]), .Cin(bit_13_cout), .Cout(bit_14_cout), .Sum(Sum[14]));
  Adder_1_bit bit_7 (.a(a[7]), .b(b[7]), .Cin(bit_6_cout), .Cout(bit_7_cout), .Sum(Sum[7]));
  Adder_1_bit bit_15 (.a(a[15]), .b(b[15]), .Cin(bit_14_cout), .Cout(Cout), .Sum(Sum[15]));

  // Other names for the same wires on the sheet: a0_7[7:0] = a[7:0]; a8_15[7:0] = a[15:8]; b0_7[7:0] = b[7:0];
  //   b8_15[7:0] = b[15:8]; Sum0_7[7:0] = Sum[7:0]; Sum8_15[7:0] = Sum[15:8]
endmodule

module Adder_1_bit (
  input  Cin,
  input  a,
  input  b,
  output Sum,
  output Cout
);

  wire and_1_out, and_2_out, xor_1_out;

  and and_1 (and_1_out, b, a);
  xor xor_1 (xor_1_out, a, b);
  or or_1 (Cout, and_1_out, and_2_out);
  and and_2 (and_2_out, xor_1_out, Cin);
  xor xor_2 (Sum, Cin, xor_1_out);
endmodule

module add4bit (
  input  Cin,
  input  [3:0] a,
  input  [3:0] b,
  output [3:0] Sum,
  output Cout
);

  wire bit_0_cout, bit_1_cout, bit_2_cout;

  Adder_1_bit bit_0 (.a(a[0]), .b(b[0]), .Cin(Cin), .Cout(bit_0_cout), .Sum(Sum[0]));
  Adder_1_bit bit_1 (.a(a[1]), .b(b[1]), .Cin(bit_0_cout), .Cout(bit_1_cout), .Sum(Sum[1]));
  Adder_1_bit bit_2 (.a(a[2]), .b(b[2]), .Cin(bit_1_cout), .Cout(bit_2_cout), .Sum(Sum[2]));
  Adder_1_bit bit_3 (.a(a[3]), .b(b[3]), .Cin(bit_2_cout), .Cout(Cout), .Sum(Sum[3]));
endmodule

module main (
  input  [15:0] a,
  input  Cin,
  input  [15:0] b,
  output [15:0] Sum,
  output Cout
);

  Adder_16_bit add16bit (.a(a), .Cin(Cin), .b(b), .Sum(Sum), .Cout(Cout));
endmodule
