// Logisim project register0311_1200.circ as structural Verilog: 9 circuits, main circuit main
module main (
  input  in_1,
  input  [15:0] in_2,
  input  [15:0] in_3,
  output [15:0] out_4,
  output out_5
);

  Add_Suber_16_bit add_suber_16_bit_1 (.a__rt(in_2), .Cin__Add_0(in_1), .b__rs(in_3), .Sum__rd(out_4), .Cout(out_5));
endmodule

module Tester (
  input  [3:0] in_1,
  input  [3:0] in_2,
  output [3:0] out_3
);

  assign out_3 = in_1 | in_2;  // OR_Gate or_1, 4 bits wide
endmodule

module register_file (
  input  Clock,
  input  [15:0] RDVAL__16_bit_Input,
  input  WE__Write_Enable,
  input  [2:0] RS2,
  input  Reset,
  input  [2:0] RD,
  input  [2:0] RS1,
  output [15:0] RS2VAL,
  output [15:0] RS1VAL
);

  wire decoder_1_out0, decoder_1_out1, decoder_1_out2, decoder_1_out3, decoder_1_out4, decoder_1_out5,
       decoder_1_out6, decoder_1_out7, EnT0, EnT1, EnT2, EnT3, EnT4, EnT5, EnT6, EnT7;
  wire [15:0] Register_0__16_bit_output, Register_1__16_bit_output, Register_2__16_bit_output,
       Register_3__16_bit_output, Register_4__16_bit_output, Register_5__16_bit_output,
       Register_6__16_bit_output, Register_7__16_bit_output;

  Decoder #(.select(3), .enable("false")) decoder_1 (
    .out0(decoder_1_out0), .out1(decoder_1_out1), .out2(decoder_1_out2), .out3(decoder_1_out3),
    .out4(decoder_1_out4), .out5(decoder_1_out5), .out6(decoder_1_out6), .out7(decoder_1_out7), .sel(RD));
  and and_1 (EnT0, decoder_1_out0, WE__Write_Enable);
  and and_2 (EnT1, decoder_1_out1, WE__Write_Enable);
  and and_3 (EnT2, decoder_1_out2, WE__Write_Enable);
  and and_4 (EnT3, decoder_1_out3, WE__Write_Enable);
  and and_5 (EnT4, decoder_1_out4, WE__Write_Enable);
  and and_6 (EnT5, decoder_1_out5, WE__Write_Enable);
  and and_7 (EnT6, decoder_1_out6, WE__Write_Enable);
  and and_8 (EnT7, decoder_1_out7, WE__Write_Enable);
  register Register_0 (
    .Clock_input(Clock), ._16_bit_Input(RDVAL__16_bit_Input), .Enable(EnT0), .Reset__ind_of_clock(Reset),
    ._16_bit_Output(Register_0__16_bit_output));
  register Register_1 (
    .Clock_input(Clock), ._16_bit_Input(RDVAL__16_bit_Input), .Enable(EnT1), .Reset__ind_of_clock(Reset),
    ._16_bit_Output(Register_1__16_bit_output));
  register Register_2 (
    .Clock_input(Clock), ._16_bit_Input(RDVAL__16_bit_Input), .Enable(EnT2), .Reset__ind_of_clock(Reset),
    ._16_bit_Output(Register_2__16_bit_output));
  register Register_3 (
    .Clock_input(Clock), ._16_bit_Input(RDVAL__16_bit_Input), .Enable(EnT3), .Reset__ind_of_clock(Reset),
    ._16_bit_Output(Register_3__16_bit_output));
  register Register_4 (
    .Clock_input(Clock), ._16_bit_Input(RDVAL__16_bit_Input), .Enable(EnT4), .Reset__ind_of_clock(Reset),
    ._16_bit_Output(Register_4__16_bit_output));
  register Register_5 (
    .Clock_input(Clock), ._16_bit_Input(RDVAL__16_bit_Input), .Enable(EnT5), .Reset__ind_of_clock(Reset),
    ._16_bit_Output(Register_5__16_bit_output));
  register Register_6 (
    .Clock_input(Clock), ._16_bit_Input(RDVAL__16_bit_Input), .Enable(EnT6), .Reset__ind_of_clock(Reset),
    ._16_bit_Output(Register_6__16_bit_output));
  register Register_7 (
    .Clock_input(Clock), ._16_bit_Input(RDVAL__16_bit_Input), .Enable(EnT7), .Reset__ind_of_clock(Reset),
    ._16_bit_Output(Register_7__16_bit_output));
  Multiplexer #(.select(3), .width(16), .enable("false")) multiplexer_1 (
    .in0(Register_0__16_bit_output), .in1(Register_1__16_bit_output), .in2(Register_2__16_bit_output),
    .in3(Register_3__16_bit_output), .in4(Register_4__16_bit_output), .in5(Register_5__16_bit_output),
    .in6(Register_6__16_bit_output), .in7(Register_7__16_bit_output), .out(RS2VAL), .sel(RS2));
  Multiplexer #(.select(3), .width(16), .enable("false")) multiplexer_2 (
    .in0(Register_0__16_bit_output), .in1(Register_1__16_bit_output), .in2(Register_2__16_bit_output),
    .in3(Register_3__16_bit_output), .in4(Register_4__16_bit_output), .in5(Register_5__16_bit_output),
    .in6(Register_6__16_bit_output), .in7(Register_7__16_bit_output), .out(RS1VAL), .sel(RS1));

  // Other names for the same wires on the sheet: _16InT[15:0] = RDVAL__16_bit_Input; ClkT = Clock; ResetT = Reset
endmodule

module register (
  input  Clock_input,
  input  [15:0] _16_bit_Input,
  input  Enable,
  input  Reset__ind_of_clock,
  output [15:0] _16_bit_Output
);

  D_Flip_Flop d_ff_1 (
    .clk(Clock_input), .D(_16_bit_Input[0]), .Q(_16_bit_Output[0]), .en(Enable), .reset(Reset__ind_of_clock));  // open: Qn, preset
  D_Flip_Flop d_ff_2 (
    .clk(Clock_input), .D(_16_bit_Input[1]), .Q(_16_bit_Output[1]), .en(Enable), .reset(Reset__ind_of_clock));  // open: Qn, preset
  D_Flip_Flop d_ff_3 (
    .clk(Clock_input), .D(_16_bit_Input[2]), .Q(_16_bit_Output[2]), .en(Enable), .reset(Reset__ind_of_clock));  // open: Qn, preset
  D_Flip_Flop d_ff_4 (
    .clk(Clock_input), .D(_16_bit_Input[3]), .Q(_16_bit_Output[3]), .en(Enable), .reset(Reset__ind_of_clock));  // open: Qn, preset
  D_Flip_Flop d_ff_5 (
    .clk(Clock_input), .D(_16_bit_Input[4]), .Q(_16_bit_Output[4]), .en(Enable), .reset(Reset__ind_of_clock));  // open: Qn, preset
  D_Flip_Flop d_ff_6 (
    .clk(Clock_input), .D(_16_bit_Input[5]), .Q(_16_bit_Output[5]), .en(Enable), .reset(Reset__ind_of_clock));  // open: Qn, preset
  D_Flip_Flop d_ff_7 (
    .clk(Clock_input), .D(_16_bit_Input[6]), .Q(_16_bit_Output[6]), .en(Enable), .reset(Reset__ind_of_clock));  // open: Qn, preset
  D_Flip_Flop d_ff_8 (
    .clk(Clock_input), .D(_16_bit_Input[7]), .Q(_16_bit_Output[7]), .en(Enable), .reset(Reset__ind_of_clock));  // open: Qn, preset
  D_Flip_Flop d_ff_9 (
    .clk(Clock_input), .D(_16_bit_Input[8]), .Q(_16_bit_Output[8]), .en(Enable), .reset(Reset__ind_of_clock));  // open: Qn, preset
  D_Flip_Flop d_ff_10 (
    .clk(Clock_input), .D(_16_bit_Input[9]), .Q(_16_bit_Output[9]), .en(Enable), .reset(Reset__ind_of_clock));  // open: Qn, preset
  D_Flip_Flop d_ff_11 (
    .clk(Clock_input), .D(_16_bit_Input[10]), .Q(_16_bit_Output[10]), .en(Enable), .reset(Reset__ind_of_clock));  // open: Qn, preset
  D_Flip_Flop d_ff_12 (
    .clk(Clock_input), .D(_16_bit_Input[11]), .Q(_16_bit_Output[11]), .en(Enable), .reset(Reset__ind_of_clock));  // open: Qn, preset
  D_Flip_Flop d_ff_13 (
    .clk(Clock_input), .D(_16_bit_Input[12]), .Q(_16_bit_Output[12]), .en(Enable), .reset(Reset__ind_of_clock));  // open: Qn, preset
  D_Flip_Flop d_ff_14 (
    .clk(Clock_input), .D(_16_bit_Input[13]), .Q(_16_bit_Output[13]), .en(Enable), .reset(Reset__ind_of_clock));  // open: Qn, preset
  D_Flip_Flop d_ff_15 (
    .clk(Clock_input), .D(_16_bit_Input[14]), .Q(_16_bit_Output[14]), .en(Enable), .reset(Reset__ind_of_clock));  // open: Qn, preset
  D_Flip_Flop d_ff_16 (
    .clk(Clock_input), .D(_16_bit_Input[15]), .Q(_16_bit_Output[15]), .en(Enable), .reset(Reset__ind_of_clock));  // open: Qn, preset
endmodule

module ALU_Slice (
  input  [15:0] a__rt,
  input  Add_0,
  input  [15:0] b__rs,
  input  [2:0] shamt,
  input  [15:0] Imm,
  input  in_6,
  input  [3:0] Opcode,
  output Cout,
  output [15:0] Q__rd,
  output Cout_2
);

  wire Add__0__or_Sub__1_out, decoder_1_out0, decoder_1_out1, decoder_1_out2, nor_1_out;
  wire [15:0] add_suber_16_bit_1_sum__rd, add_suber_16_bit_2_sum__rd, And__0_011_out, sll_1_rd, sra_1_rd,
       Xor__0_100_out;

  Add_Suber_16_bit add_suber_16_bit_1 (
    .a__rt(a__rt), .Cin__Add_0(Add__0__or_Sub__1_out), .b__rs(b__rs), .Sum__rd(add_suber_16_bit_1_sum__rd),
    .Cout(Cout));
  Add_Suber_16_bit add_suber_16_bit_2 (
    .a__rt(Imm), .Cin__Add_0(Add_0), .b__rs(b__rs), .Sum__rd(add_suber_16_bit_2_sum__rd), .Cout(Cout_2));
  assign And__0_011_out = a__rt & b__rs;  // AND_Gate And__0_011, 16 bits wide
  assign Xor__0_100_out = a__rt ^ b__rs;  // XOR_Gate Xor__0_100, 16 bits wide
  SLL sll_1 (.rs(b__rs), ._0_In(in_6), .shamt(shamt), .rd(sll_1_rd));
  SRA sra_1 (.rs(b__rs), .shamt(shamt), .rd(sra_1_rd));
  Multiplexer #(.select(3), .width(16), .enable("false")) multiplexer_1 (
    .in0(add_suber_16_bit_1_sum__rd), .in1(add_suber_16_bit_2_sum__rd), .in2(add_suber_16_bit_1_sum__rd),
    .in3(And__0_011_out), .in4(Xor__0_100_out), .in5(sll_1_rd), .in6(sra_1_rd), .out(Q__rd), .sel(Opcode[2:0]));  // open: in7
  Decoder #(.select(3), .enable("false")) decoder_1 (
    .out0(decoder_1_out0), .out1(decoder_1_out1), .out2(decoder_1_out2), .sel(Opcode[2:0]));  // open: out3, out4, out5, out6, out7
  nor nor_1 (nor_1_out, decoder_1_out0, decoder_1_out1);
  or Add__0__or_Sub__1 (Add__0__or_Sub__1_out, nor_1_out, decoder_1_out2);

  // Other names for the same wires on the sheet: a[15:0] = a__rt; b[15:0] = b__rs
endmodule

module Add_Suber_16_bit (
  input  [15:0] a__rt,
  input  Cin__Add_0,
  input  [15:0] b__rs,
  output [15:0] Sum__rd,
  output Cout
);

  wire bit_0_cout, bit_1_cout, bit_2_cout, bit_3_cout, bit_4_cout, bit_5_cout, bit_6_cout, bit_7_cout,
       bit_8_cout, bit_9_cout, bit_10_cout, bit_11_cout, bit_12_cout, bit_13_cout, bit_14_cout, xor_1_out,
       xor_2_out, xor_3_out, xor_4_out, xor_5_out, xor_6_out, xor_7_out, xor_8_out, xor_9_out, xor_10_out,
       xor_11_out, xor_12_out, xor_13_out, xor_14_out, xor_15_out, xor_16_out;

  Adder_1_bit bit_0 (.a(xor_1_out), .b(b__rs[0]), .Cin(Cin__Add_0), .Cout(bit_0_cout), .Sum(Sum__rd[0]));
  xor xor_1 (xor_1_out, Cin__Add_0, a__rt[0]);
  Adder_1_bit bit_8 (.a(xor_2_out), .b(b__rs[8]), .Cin(bit_7_cout), .Cout(bit_8_cout), .Sum(Sum__rd[8]));
  xor xor_2 (xor_2_out, Cin__Add_0, a__rt[8]);
  Adder_1_bit bit_1 (.a(xor_3_out), .b(b__rs[1]), .Cin(bit_0_cout), .Cout(bit_1_cout), .Sum(Sum__rd[1]));
  xor xor_3 (xor_3_out, Cin__Add_0, a__rt[1]);
  Adder_1_bit bit_9 (.a(xor_4_out), .b(b__rs[9]), .Cin(bit_8_cout), .Cout(bit_9_cout), .Sum(Sum__rd[9]));
  xor xor_4 (xor_4_out, Cin__Add_0, a__rt[9]);
  Adder_1_bit bit_2 (.a(xor_5_out), .b(b__rs[2]), .Cin(bit_1_cout), .Cout(bit_2_cout), .Sum(Sum__rd[2]));
  xor xor_5 (xor_5_out, Cin__Add_0, a__rt[2]);
  Adder_1_bit bit_10 (.a(xor_6_out), .b(b__rs[10]), .Cin(bit_9_cout), .Cout(bit_10_cout), .Sum(Sum__rd[10]));
  xor xor_6 (xor_6_out, Cin__Add_0, a__rt[10]);
  Adder_1_bit bit_3 (.a(xor_7_out), .b(b__rs[3]), .Cin(bit_2_cout), .Cout(bit_3_cout), .Sum(Sum__rd[3]));
  xor xor_7 (xor_7_out, Cin__Add_0, a__rt[3]);
  Adder_1_bit bit_11 (.a(xor_8_out), .b(b__rs[11]), .Cin(bit_10_cout), .Cout(bit_11_cout), .Sum(Sum__rd[11]));
  xor xor_8 (xor_8_out, Cin__Add_0, a__rt[11]);
  xor xor_9 (xor_9_out, Cin__Add_0, a__rt[4]);
  xor xor_10 (xor_10_out, Cin__Add_0, a__rt[12]);
  Adder_1_bit bit_4 (.a(xor_9_out), .b(b__rs[4]), .Cin(bit_3_cout), .Cout(bit_4_cout), .Sum(Sum__rd[4]));
  Adder_1_bit bit_12 (.a(xor_10_out), .b(b__rs[12]), .Cin(bit_11_cout), .Cout(bit_12_cout), .Sum(Sum__rd[12]));
  Adder_1_bit bit_5 (.a(xor_11_out), .b(b__rs[5]), .Cin(bit_4_cout), .Cout(bit_5_cout), .Sum(Sum__rd[5]));
  xor xor_11 (xor_11_out, Cin__Add_0, a__rt[5]);
  Adder_1_bit bit_13 (.a(xor_12_out), .b(b__rs[13]), .Cin(bit_12_cout), .Cout(bit_13_cout), .Sum(Sum__rd[13]));
  xor xor_12 (xor_12_out, Cin__Add_0, a__rt[13]);
  Adder_1_bit bit_6 (.a(xor_13_out), .b(b__rs[6]), .Cin(bit_5_cout), .Cout(bit_6_cout), .Sum(Sum__rd[6]));
  xor xor_13 (xor_13_out, Cin__Add_0, a__rt[6]);
  Adder_1_bit bit_14 (.a(xor_14_out), .b(b__rs[14]), .Cin(bit_13_cout), .Cout(bit_14_cout), .Sum(Sum__rd[14]));
  xor xor_14 (xor_14_out, Cin__Add_0, a__rt[14]);
  xor xor_15 (xor_15_out, Cin__Add_0, a__rt[7]);
  xor xor_16 (xor_16_out, Cin__Add_0, a__rt[15]);
  Adder_1_bit bit_7 (.a(xor_15_out), .b(b__rs[7]), .Cin(bit_6_cout), .Cout(bit_7_cout), .Sum(Sum__rd[7]));
  Adder_1_bit bit_15 (.a(xor_16_out), .b(b__rs[15]), .Cin(bit_14_cout), .Cout(Cout), .Sum(Sum__rd[15]));

  // Other names for the same wires on the sheet: a0_7[7:0] = a__rt[7:0]; a8_15[7:0] = a__rt[15:8];
  //   b0_7[7:0] = b__rs[7:0]; b8_15[7:0] = b__rs[15:8]; Sum0_7[7:0] = Sum__rd[7:0]; Sum8_15[7:0] = Sum__rd[15:8]
endmodule

module Adder_1_bit (
  input  Cin,
  input  a,
  input  b,
  output Sum,
  output Cout
);

  wire and_1_out, and_2_out, xor_1_out;

  and and_1 (and_1_out, b, a);
  xor xor_1 (xor_1_out, a, b);
  or or_1 (Cout, and_1_out, and_2_out);
  and and_2 (and_2_out, xor_1_out, Cin);
  xor xor_2 (Sum, Cin, xor_1_out);
endmodule

module SLL (
  input  [15:0] rs,
  input  _0_In,
  input  [2:0] shamt,
  output [15:0] rd
);

  wire multiplexer_1_out, multiplexer_2_out, multiplexer_3_out, multiplexer_4_out, multiplexer_5_out,
       multiplexer_6_out, multiplexer_7_out, multiplexer_8_out, multiplexer_9_out, multiplexer_10_out,
       multiplexer_11_out, multiplexer_12_out, multiplexer_13_out, multiplexer_14_out, multiplexer_15_out,
       multiplexer_16_out, multiplexer_17_out, multiplexer_18_out, multiplexer_19_out, multiplexer_20_out,
       multiplexer_21_out, multiplexer_22_out, multiplexer_23_out, multiplexer_24_out, multiplexer_25_out,
       multiplexer_26_out, multiplexer_27_out, multiplexer_28_out, multiplexer_29_out, multiplexer_30_out,
       multiplexer_31_out, multiplexer_32_out;

  Multiplexer #(.enable("false")) multiplexer_1 (.in0(rs[15]), .in1(rs[14]), .out(multiplexer_1_out), .sel(shamt[0]));
  Multiplexer #(.enable("false")) multiplexer_2 (.in0(rs[14]), .in1(rs[13]), .out(multiplexer_2_out), .sel(shamt[0]));
  Multiplexer #(.enable("false")) multiplexer_3 (.in0(rs[13]), .in1(rs[12]), .out(multiplexer_3_out), .sel(shamt[0]));
  Multiplexer #(.enable("false")) multiplexer_4 (.in0(rs[12]), .in1(rs[11]), .out(multiplexer_4_out), .sel(shamt[0]));
  Multiplexer #(.enable("false")) multiplexer_5 (.in0(rs[11]), .in1(rs[10]), .out(multiplexer_5_out), .sel(shamt[0]));
  Multiplexer #(.enable("false")) multiplexer_6 (.in0(rs[10]), .in1(rs[9]), .out(multiplexer_6_out), .sel(shamt[0]));
  Multiplexer #(.enable("false")) multiplexer_7 (.in0(rs[9]), .in1(rs[8]), .out(multiplexer_7_out), .sel(shamt[0]));
  Multiplexer #(.enable("false")) multiplexer_8 (.in0(rs[8]), .in1(rs[7]), .out(multiplexer_8_out), .sel(shamt[0]));
  Multiplexer #(.enable("false")) multiplexer_9 (.in0(rs[7]), .in1(rs[6]), .out(multiplexer_9_out), .sel(shamt[0]));
  Multiplexer #(.enable("false")) multiplexer_10 (.in0(rs[6]), .in1(rs[5]), .out(multiplexer_10_out), .sel(shamt[0]));
  Multiplexer #(.enable("false")) multiplexer_11 (.in0(rs[5]), .in1(rs[4]), .out(multiplexer_11_out), .sel(shamt[0]));
  Multiplexer #(.enable("false")) multiplexer_12 (.in0(rs[4]), .in1(rs[3]), .out(multiplexer_12_out), .sel(shamt[0]));
  Multiplexer #(.enable("false")) multiplexer_13 (.in0(rs[3]), .in1(rs[2]), .out(multiplexer_13_out), .sel(shamt[0]));
  Multiplexer #(.enable("false")) multiplexer_14 (.in0(rs[2]), .in1(rs[1]), .out(multiplexer_14_out), .sel(shamt[0]));
  Multiplexer #(.enable("false")) multiplexer_15 (.in0(rs[1]), .in1(rs[0]), .out(multiplexer_15_out), .sel(shamt[0]));
  Multiplexer #(.enable("false")) multiplexer_16 (.in0(rs[0]), .in1(_0_In), .out(multiplexer_16_out), .sel(shamt[0]));
  Multiplexer #(.enable("false")) multiplexer_17 (
    .in0(multiplexer_1_out), .in1(multiplexer_3_out), .out(multiplexer_17_out), .sel(shamt[1]));
  Multiplexer #(.enable("false")) multiplexer_18 (
    .in0(multiplexer_2_out), .in1(multiplexer_4_out), .out(multiplexer_18_out), .sel(shamt[1]));
  Multiplexer #(.enable("false")) multiplexer_19 (
    .in0(multiplexer_3_out), .in1(multiplexer_5_out), .out(multiplexer_19_out), .sel(shamt[1]));
  Multiplexer #(.enable("false")) multiplexer_20 (
    .in0(multiplexer_4_out), .in1(multiplexer_6_out), .out(multiplexer_20_out), .sel(shamt[1]));
  Multiplexer #(.enable("false")) multiplexer_21 (
    .in0(multiplexer_5_out), .in1(multiplexer_7_out), .out(multiplexer_21_out), .sel(shamt[1]));
  Multiplexer #(.enable("false")) multiplexer_22 (
    .in0(multiplexer_6_out), .in1(multiplexer_8_out), .out(multiplexer_22_out), .sel(shamt[1]));
  Multiplexer #(.enable("false")) multiplexer_23 (
    .in0(multiplexer_7_out), .in1(multiplexer_9_out), .out(multiplexer_23_out), .sel(shamt[1]));
  Multiplexer #(.enable("false")) multiplexer_24 (
    .in0(multiplexer_8_out), .in1(multiplexer_10_out), .out(multiplexer_24_out), .sel(shamt[1]));
  Multiplexer #(.enable("false")) multiplexer_25 (
    .in0(multiplexer_9_out), .in1(multiplexer_11_out), .out(multiplexer_25_out), .sel(shamt[1]));
  Multiplexer #(.enable("false")) multiplexer_26 (
    .in0(multiplexer_10_out), .in1(multiplexer_12_out), .out(multiplexer_26_out), .sel(shamt[1]));
  Multiplexer #(.enable("false")) multiplexer_27 (
    .in0(multiplexer_11_out), .in1(multiplexer_13_out), .out(multiplexer_27_out), .sel(shamt[1]));
  Multiplexer #(.enable("false")) multiplexer_28 (
    .in0(multiplexer_12_out), .in1(multiplexer_14_out), .out(multiplexer_28_out), .sel(shamt[1]));
  Multiplexer #(.enable("false")) multiplexer_29 (
    .in0(multiplexer_13_out), .in1(multiplexer_15_out), .out(multiplexer_29_out), .sel(shamt[1]));
  Multiplexer #(.enable("false")) multiplexer_30 (
    .in0(multiplexer_14_out), .in1(multiplexer_16_out), .out(multiplexer_30_out), .sel(shamt[1]));
  Multiplexer #(.enable("false")) multiplexer_31 (
    .in0(multiplexer_15_out), .in1(_0_In), .out(multiplexer_31_out), .sel(shamt[1]));
  Multiplexer #(.enable("false")) multiplexer_32 (
    .in0(multiplexer_16_out), .in1(_0_In), .out(multiplexer_32_out), .sel(shamt[1]));
  Multiplexer #(.enable("false")) multiplexer_33 (
    .in0(multiplexer_17_out), .in1(multiplexer_21_out), .out(rd[15]), .sel(shamt[2]));
  Multiplexer #(.enable("false")) multiplexer_34 (
    .in0(multiplexer_18_out), .in1(multiplexer_22_out), .out(rd[14]), .sel(shamt[2]));
  Multiplexer #(.enable("false")) multiplexer_35 (
    .in0(multiplexer_19_out), .in1(multiplexer_23_out), .out(rd[13]), .sel(shamt[2]));
  Multiplexer #(.enable("false")) multiplexer_36 (
    .in0(multiplexer_20_out), .in1(multiplexer_24_out), .out(rd[12]), .sel(shamt[2]));
  Multiplexer #(.enable("false")) multiplexer_37 (
    .in0(multiplexer_21_out), .in1(multiplexer_25_out), .out(rd[11]), .sel(shamt[2]));
  Multiplexer #(.enable("false")) multiplexer_38 (
    .in0(multiplexer_22_out), .in1(multiplexer_26_out), .out(rd[10]), .sel(shamt[2]));
  Multiplexer #(.enable("false")) multiplexer_39 (
    .in0(multiplexer_23_out), .in1(multiplexer_27_out), .out(rd[9]), .sel(shamt[2]));
  Multiplexer #(.enable("false")) multiplexer_40 (
    .in0(multiplexer_24_out), .in1(multiplexer_28_out), .out(rd[8]), .sel(shamt[2]));
  Multiplexer #(.enable("false")) multiplexer_41 (
    .in0(multiplexer_25_out), .in1(multiplexer_29_out), .out(rd[7]), .sel(shamt[2]));
  Multiplexer #(.enable("false")) multiplexer_42 (
    .in0(multiplexer_26_out), .in1(multiplexer_30_out), .out(rd[6]), .sel(shamt[2]));
  Multiplexer #(.enable("false")) multiplexer_43 (
    .in0(multiplexer_27_out), .in1(multiplexer_31_out), .out(rd[5]), .sel(shamt[2]));
  Multiplexer #(.enable("false")) multiplexer_44 (
    .in0(multiplexer_28_out), .in1(multiplexer_32_out), .out(rd[4]), .sel(shamt[2]));
  Multiplexer #(.enable("false")) multiplexer_45 (.in0(multiplexer_29_out), .in1(_0_In), .out(rd[3]), .sel(shamt[2]));
  Multiplexer #(.enable("false")) multiplexer_46 (.in0(multiplexer_30_out), .in1(_0_In), .out(rd[2]), .sel(shamt[2]));
  Multiplexer #(.enable("false")) multiplexer_47 (.in0(multiplexer_31_out), .in1(_0_In), .out(rd[1]), .sel(shamt[2]));
  Multiplexer #(.enable("false")) multiplexer_48 (.in0(multiplexer_32_out), .in1(_0_In), .out(rd[0]), .sel(shamt[2]));
endmodule

module SRA (
  input  [15:0] rs,
  input  [2:0] shamt,
  output [15:0] rd
);

  wire multiplexer_1_out, multiplexer_2_out, multiplexer_3_out, multiplexer_4_out, multiplexer_5_out,
       multiplexer_6_out, multiplexer_7_out, multiplexer_8_out, multiplexer_9_out, multiplexer_10_out,
       multiplexer_11_out, multiplexer_12_out, multiplexer_13_out, multiplexer_14_out, multiplexer_15_out,
       multiplexer_16_out, multiplexer_17_out, multiplexer_18_out, multiplexer_19_out, multiplexer_20_out,
       multiplexer_21_out, multiplexer_22_out, multiplexer_23_out, multiplexer_24_out, multiplexer_25_out,
       multiplexer_26_out, multiplexer_27_out, multiplexer_28_out, multiplexer_29_out, multiplexer_30_out,
       multiplexer_31_out, multiplexer_32_out;

  Multiplexer #(.enable("false")) multiplexer_1 (.in0(rs[0]), .in1(rs[1]), .out(multiplexer_1_out), .sel(shamt[0]));
  Multiplexer #(.enable("false")) multiplexer_2 (.in0(rs[1]), .in1(rs[2]), .out(multiplexer_2_out), .sel(shamt[0]));
  Multiplexer #(.enable("false")) multiplexer_3 (.in0(rs[2]), .in1(rs[3]), .out(multiplexer_3_out), .sel(shamt[0]));
  Multiplexer #(.enable("false")) multiplexer_4 (.in0(rs[3]), .in1(rs[4]), .out(multiplexer_4_out), .sel(shamt[0]));
  Multiplexer #(.enable("false")) multiplexer_5 (.in0(rs[4]), .in1(rs[5]), .out(multiplexer_5_out), .sel(shamt[0]));
  Multiplexer #(.enable("false")) multiplexer_6 (.in0(rs[5]), .in1(rs[6]), .out(multiplexer_6_out), .sel(shamt[0]));
  Multiplexer #(.enable("false")) multiplexer_7 (.in0(rs[6]), .in1(rs[7]), .out(multiplexer_7_out), .sel(shamt[0]));
  Multiplexer #(.enable("false")) multiplexer_8 (.in0(rs[7]), .in1(rs[8]), .out(multiplexer_8_out), .sel(shamt[0]));
  Multiplexer #(.enable("false")) multiplexer_9 (.in0(rs[8]), .in1(rs[9]), .out(multiplexer_9_out), .sel(shamt[0]));
  Multiplexer #(.enable("false")) multiplexer_10 (.in0(rs[9]), .in1(rs[10]), .out(multiplexer_10_out), .sel(shamt[0]));
  Multiplexer #(.enable("false")) multiplexer_11 (.in0(rs[10]), .in1(rs[11]), .out(multiplexer_11_out), .sel(shamt[0]));
  Multiplexer #(.enable("false")) multiplexer_12 (.in0(rs[11]), .in1(rs[12]), .out(multiplexer_12_out), .sel(shamt[0]));
  Multiplexer #(.enable("false")) multiplexer_13 (.in0(rs[12]), .in1(rs[13]), .out(multiplexer_13_out), .sel(shamt[0]));
  Multiplexer #(.enable("false")) multiplexer_14 (.in0(rs[13]), .in1(rs[14]), .out(multiplexer_14_out), .sel(shamt[0]));
  Multiplexer #(.enable("false")) multiplexer_15 (.in0(rs[14]), .in1(rs[15]), .out(multiplexer_15_out), .sel(shamt[0]));
  Multiplexer #(.enable("false")) multiplexer_16 (.in0(rs[15]), .in1(rs[15]), .out(multiplexer_16_out), .sel(shamt[0]));
  Multiplexer #(.enable("false")) multiplexer_17 (
    .in0(multiplexer_1_out), .in1(multiplexer_3_out), .out(multiplexer_17_out), .sel(shamt[1]));
  Multiplexer #(.enable("false")) multiplexer_18 (
    .in0(multiplexer_2_out), .in1(multiplexer_4_out), .out(multiplexer_18_out), .sel(shamt[1]));
  Multiplexer #(.enable("false")) multiplexer_19 (
    .in0(multiplexer_3_out), .in1(multiplexer_5_out), .out(multiplexer_19_out), .sel(shamt[1]));
  Multiplexer #(.enable("false")) multiplexer_20 (
    .in0(multiplexer_4_out), .in1(multiplexer_6_out), .out(multiplexer_20_out), .sel(shamt[1]));
  Multiplexer #(.enable("false")) multiplexer_21 (
    .in0(multiplexer_5_out), .in1(multiplexer_7_out), .out(multiplexer_21_out), .sel(shamt[1]));
  Multiplexer #(.enable("false")) multiplexer_22 (
    .in0(multiplexer_6_out), .in1(multiplexer_8_out), .out(multiplexer_22_out), .sel(shamt[1]));
  Multiplexer #(.enable("false")) multiplexer_23 (
    .in0(multiplexer_7_out), .in1(multiplexer_9_out), .out(multiplexer_23_out), .sel(shamt[1]));
  Multiplexer #(.enable("false")) multiplexer_24 (
    .in0(multiplexer_8_out), .in1(multiplexer_10_out), .out(multiplexer_24_out), .sel(shamt[1]));
  Multiplexer #(.enable("false")) multiplexer_25 (
    .in0(multiplexer_9_out), .in1(multiplexer_11_out), .out(multiplexer_25_out), .sel(shamt[1]));
  Multiplexer #(.enable("false")) multiplexer_26 (
    .in0(multiplexer_10_out), .in1(multiplexer_12_out), .out(multiplexer_26_out), .sel(shamt[1]));
  Multiplexer #(.enable("false")) multiplexer_27 (
    .in0(multiplexer_11_out), .in1(multiplexer_13_out), .out(multiplexer_27_out), .sel(shamt[1]));
  Multiplexer #(.enable("false")) multiplexer_28 (
    .in0(multiplexer_12_out), .in1(multiplexer_14_out), .out(multiplexer_28_out), .sel(shamt[1]));
  Multiplexer #(.enable("false")) multiplexer_29 (
    .in0(multiplexer_13_out), .in1(multiplexer_15_out), .out(multiplexer_29_out), .sel(shamt[1]));
  Multiplexer #(.enable("false")) multiplexer_30 (
    .in0(multiplexer_14_out), .in1(multiplexer_16_out), .out(multiplexer_30_out), .sel(shamt[1]));
  Multiplexer #(.enable("false")) multiplexer_31 (
    .in0(multiplexer_15_out), .in1(rs[15]), .out(multiplexer_31_out), .sel(shamt[1]));
  Multiplexer #(.enable("false")) multiplexer_32 (
    .in0(multiplexer_16_out), .in1(rs[15]), .out(multiplexer_32_out), .sel(shamt[1]));
  Multiplexer #(.enable("false")) multiplexer_33 (
    .in0(multiplexer_17_out), .in1(multiplexer_21_out), .out(rd[0]), .sel(shamt[2]));
  Multiplexer #(.enable("false")) multiplexer_34 (
    .in0(multiplexer_18_out), .in1(multiplexer_22_out), .out(rd[1]), .sel(shamt[2]));
  Multiplexer #(.enable("false")) multiplexer_35 (
    .in0(multiplexer_19_out), .in1(multiplexer_23_out), .out(rd[2]), .sel(shamt[2]));
  Multiplexer #(.enable("false")) multiplexer_36 (
    .in0(multiplexer_20_out), .in1(multiplexer_24_out), .out(rd[3]), .sel(shamt[2]));
  Multiplexer #(.enable("false")) multiplexer_37 (
    .in0(multiplexer_21_out), .in1(multiplexer_25_out), .out(rd[4]), .sel(shamt[2]));
  Multiplexer #(.enable("false")) multiplexer_38 (
    .in0(multiplexer_22_out), .in1(multiplexer_26_out), .out(rd[5]), .sel(shamt[2]));
  Multiplexer #(.enable("false")) multiplexer_39 (
    .in0(multiplexer_23_out), .in1(multiplexer_27_out), .out(rd[6]), .sel(shamt[2]));
  Multiplexer #(.enable("false")) multiplexer_40 (
    .in0(multiplexer_24_out), .in1(multiplexer_28_out), .out(rd[7]), .sel(shamt[2]));
  Multiplexer #(.enable("false")) multiplexer_41 (
    .in0(multiplexer_25_out), .in1(multiplexer_29_out), .out(rd[8]), .sel(shamt[2]));
  Multiplexer #(.enable("false")) multiplexer_42 (
    .in0(multiplexer_26_out), .in1(multiplexer_30_out), .out(rd[9]), .sel(shamt[2]));
  Multiplexer #(.enable("false")) multiplexer_43 (
    .in0(multiplexer_27_out), .in1(multiplexer_31_out), .out(rd[10]), .sel(shamt[2]));
  Multiplexer #(.enable("false")) multiplexer_44 (
    .in0(multiplexer_28_out), .in1(multiplexer_32_out), .out(rd[11]), .sel(shamt[2]));
  Multiplexer #(.enable("false")) multiplexer_45 (.in0(multiplexer_29_out), .in1(rs[15]), .out(rd[12]), .sel(shamt[2]));
  Multiplexer #(.enable("false")) multiplexer_46 (.in0(multiplexer_30_out), .in1(rs[15]), .out(rd[13]), .sel(shamt[2]));
  Multiplexer #(.enable("false")) multiplexer_47 (.in0(multiplexer_31_out), .in1(rs[15]), .out(rd[14]), .sel(shamt[2]));
  Multiplexer #(.enable("false")) multiplexer_48 (.in0(multiplexer_32_out), .in1(rs[15]), .out(rd[15]), .sel(shamt[2]));
endmodule
