// Logisim project register - Copy.circ as structural Verilog
module register (
  input  Clock_input,
  input  [15:0] _16_bit_Input,
  input  Enable,
  input  Reset__ind_of_clock,
  output [15:0] _16_bit_Output
);

  D_Flip_Flop d_ff_1 (
    .clk(Clock_input), .D(_16_bit_Input[0]), .Q(_16_bit_Output[0]), .en(Enable), .reset(Reset__ind_of_clock));  // open: Qn, preset
  D_Flip_Flop d_ff_2 (
    .clk(Clock_input), .D(_16_bit_Input[1]), .Q(_16_bit_Output[1]), .en(Enable), .reset(Reset__ind_of_clock));  // open: Qn, preset
  D_Flip_Flop d_ff_3 (
    .clk(Clock_input), .D(_16_bit_Input[2]), .Q(_16_bit_Output[2]), .en(Enable), .reset(Reset__ind_of_clock));  // open: Qn, preset
  D_Flip_Flop d_ff_4 (
    .clk(Clock_input), .D(_16_bit_Input[3]), .Q(_16_bit_Output[3]), .en(Enable), .reset(Reset__ind_of_clock));  // open: Qn, preset
  D_Flip_Flop d_ff_5 (
    .clk(Clock_input), .D(_16_bit_Input[4]), .Q(_16_bit_Output[4]), .en(Enable), .reset(Reset__ind_of_clock));  // open: Qn, preset
  D_Flip_Flop d_ff_6 (
    .clk(Clock_input), .D(_16_bit_Input[5]), .Q(_16_bit_Output[5]), .en(Enable), .reset(Reset__ind_of_clock));  // open: Qn, preset
  D_Flip_Flop d_ff_7 (
    .clk(Clock_input), .D(_16_bit_Input[6]), .Q(_16_bit_Output[6]), .en(Enable), .reset(Reset__ind_of_clock));  // open: Qn, preset
  D_Flip_Flop d_ff_8 (
    .clk(Clock_input), .D(_16_bit_Input[7]), .Q(_16_bit_Output[7]), .en(Enable), .reset(Reset__ind_of_clock));  // open: Qn, preset
  D_Flip_Flop d_ff_9 (
    .clk(Clock_input), .D(_16_bit_Input[8]), .Q(_16_bit_Output[8]), .en(Enable), .reset(Reset__ind_of_clock));  // open: Qn, preset
  D_Flip_Flop d_ff_10 (
    .clk(Clock_input), .D(_16_bit_Input[9]), .Q(_16_bit_Output[9]), .en(Enable), .reset(Reset__ind_of_clock));  // open: Qn, preset
  D_Flip_Flop d_ff_11 (
    .clk(Clock_input), .D(_16_bit_Input[10]), .Q(_16_bit_Output[10]), .en(Enable), .reset(Reset__ind_of_clock));  // open: Qn, preset
  D_Flip_Flop d_ff_12 (
    .clk(Clock_input), .D(_16_bit_Input[11]), .Q(_16_bit_Output[11]), .en(Enable), .reset(Reset__ind_of_clock));  // open: Qn, preset
  D_Flip_Flop d_ff_13 (
    .clk(Clock_input), .D(_16_bit_Input[12]), .Q(_16_bit_Output[12]), .en(Enable), .reset(Reset__ind_of_clock));  // open: Qn, preset
  D_Flip_Flop d_ff_14 (
    .clk(Clock_input), .D(_16_bit_Input[13]), .Q(_16_bit_Output[13]), .en(Enable), .reset(Reset__ind_of_clock));  // open: Qn, preset
  D_Flip_Flop d_ff_15 (
    .clk(Clock_input), .D(_16_bit_Input[14]), .Q(_16_bit_Output[14]), .en(Enable), .reset(Reset__ind_of_clock));  // open: Qn, preset
  D_Flip_Flop d_ff_16 (
    .clk(Clock_input), .D(_16_bit_Input[15]), .Q(_16_bit_Output[15]), .en(Enable), .reset(Reset__ind_of_clock));  // open: Qn, preset
endmodule

module register_file (
  input  Clock,
  input  [15:0] RDVAL__16_bit_Input,
  input  WE__Write_Enable,
  input  [2:0] RS2,
  input  Reset,
  input  [2:0] RD,
  input  [2:0] RS1,
  output [15:0] RS2VAL,
  output [15:0] RS1VAL
);

  wire decoder_1_out0, decoder_1_out1, decoder_1_out2, decoder_1_out3, decoder_1_out4, decoder_1_out5,
       decoder_1_out6, decoder_1_out7, EnT0, EnT1, EnT2, EnT3, EnT4, EnT5, EnT6, EnT7;
  wire [15:0] Register_0__16_bit_output, Register_1__16_bit_output, Register_2__16_bit_output,
       Register_3__16_bit_output, Register_4__16_bit_output, Register_5__16_bit_output,
       Register_6__16_bit_output, Register_7__16_bit_output;

  Decoder #(.select(3), .enable("false")) decoder_1 (
    .out0(decoder_1_out0), .out1(decoder_1_out1), .out2(decoder_1_out2), .out3(decoder_1_out3),
    .out4(decoder_1_out4), .out5(decoder_1_out5), .out6(decoder_1_out6), .out7(decoder_1_out7), .sel(RD));
  and and_1 (EnT0, decoder_1_out0, WE__Write_Enable);
  and and_2 (EnT1, decoder_1_out1, WE__Write_Enable);
  and and_3 (EnT2, decoder_1_out2, WE__Write_Enable);
  and and_4 (EnT3, decoder_1_out3, WE__Write_Enable);
  and and_5 (EnT4, decoder_1_out4, WE__Write_Enable);
  and and_6 (EnT5, decoder_1_out5, WE__Write_Enable);
  and and_7 (EnT6, decoder_1_out6, WE__Write_Enable);
  and and_8 (EnT7, decoder_1_out7, WE__Write_Enable);
  register Register_0 (
    .Clock_input(Clock), ._16_bit_Input(RDVAL__16_bit_Input), .Enable(EnT0), .Reset__ind_of_clock(Reset),
    ._16_bit_Output(Register_0__16_bit_output));
  register Register_1 (
    .Clock_input(Clock), ._16_bit_Input(RDVAL__16_bit_Input), .Enable(EnT1), .Reset__ind_of_clock(Reset),
    ._16_bit_Output(Register_1__16_bit_output));
  register Register_2 (
    .Clock_input(Clock), ._16_bit_Input(RDVAL__16_bit_Input), .Enable(EnT2), .Reset__ind_of_clock(Reset),
    ._16_bit_Output(Register_2__16_bit_output));
  register Register_3 (
    .Clock_input(Clock), ._16_bit_Input(RDVAL__16_bit_Input), .Enable(EnT3), .Reset__ind_of_clock(Reset),
    ._16_bit_Output(Register_3__16_bit_output));
  register Register_4 (
    .Clock_input(Clock), ._16_bit_Input(RDVAL__16_bit_Input), .Enable(EnT4), .Reset__ind_of_clock(Reset),
    ._16_bit_Output(Register_4__16_bit_output));
  register Register_5 (
    .Clock_input(Clock), ._16_bit_Input(RDVAL__16_bit_Input), .Enable(EnT5), .Reset__ind_of_clock(Reset),
    ._16_bit_Output(Register_5__16_bit_output));
  register Register_6 (
    .Clock_input(Clock), ._16_bit_Input(RDVAL__16_bit_Input), .Enable(EnT6), .Reset__ind_of_clock(Reset),
    ._16_bit_Output(Register_6__16_bit_output));
  register Register_7 (
    .Clock_input(Clock), ._16_bit_Input(RDVAL__16_bit_Input), .Enable(EnT7), .Reset__ind_of_clock(Reset),
    ._16_bit_Output(Register_7__16_bit_output));
  Multiplexer #(.select(3), .width(16), .enable("false")) multiplexer_1 (
    .in0(Register_0__16_bit_output), .in1(Register_1__16_bit_output), .in2(Register_2__16_bit_output),
    .in3(Register_3__16_bit_output), .in4(Register_4__16_bit_output), .in5(Register_5__16_bit_output),
    .in6(Register_6__16_bit_output), .in7(Register_7__16_bit_output), .out(RS2VAL), .sel(RS2));
  Multiplexer #(.select(3), .width(16), .enable("false")) multiplexer_2 (
    .in0(Register_0__16_bit_output), .in1(Register_1__16_bit_output), .in2(Register_2__16_bit_output),
    .in3(Register_3__16_bit_output), .in4(Register_4__16_bit_output), .in5(Register_5__16_bit_output),
    .in6(Register_6__16_bit_output), .in7(Register_7__16_bit_output), .out(RS1VAL), .sel(RS1));

  // Other names for the same wires on the sheet: _16InT[15:0] = RDVAL__16_bit_Input; ClkT = Clock; ResetT = Reset
endmodule
