// Logisim project register.circ as structural Verilog: 15 circuits, main circuit main
module main (
  input  in_1,
  input  [15:0] in_2,
  input  [15:0] in_3,
  input  [15:0] in_4,
  input  [15:0] in_5,
  output [15:0] out_6,
  output out_7,
  output [15:0] out_8
);

  Add_Suber_16_bit add_suber_16_bit_1 (.a__rt(in_2), .Cin__Add_0(in_1), .b__rs(in_3), .Sum__rd(out_6), .Cout(out_7));
  assign out_8 = in_4 & in_5;  // AND_Gate and_1, 16 bits wide
endmodule

module processor (
  input  Reset,
  output out_2
);

  wire and_1_out, beq_out, blt, blt_out, Clk, Cout, Eq_0_out, \input , instr_dec_1_i_type, instr_dec_1_lw,
       instr_dec_1_r_type, instr_dec_1_sw, J_type, jal, jr, not_1_out, not_2_out, not_3_out, not_4_out,
       not_5_out, not_6_out, not_7_out, not_8_out, not_9_out, not_10_out, not_11_out, not_12_out, not_13_out,
       not_14_out, not_15_out, not_16_out, not_17_out, not_18_out, not_19_out, not_20_out, or_1_out,
       \output , WE;
  wire [2:0] multiplexer_3_out, multiplexer_4_out, multiplexer_5_out;
  wire [3:0] Op, register_file_1_r1, register_file_1_r1_2, register_file_1_r1_3, register_file_1_r1_4,
       register_file_1_r2, register_file_1_r2_2, register_file_1_r2_3, register_file_1_r2_4,
       register_file_1_r3, register_file_1_r3_2, register_file_1_r3_3, register_file_1_r3_4,
       register_file_1_r4, register_file_1_r4_2, register_file_1_r4_3, register_file_1_r4_4,
       register_file_1_r5, register_file_1_r5_2, register_file_1_r5_3, register_file_1_r5_4,
       register_file_1_r6, register_file_1_r6_2, register_file_1_r6_3, register_file_1_r6_4,
       register_file_1_r7, register_file_1_r7_2, register_file_1_r7_3, register_file_1_r7_4;
  wire [11:0] Addr;
  wire [15:0] add_suber_16_bit_1_sum__rd, add_suber_16_bit_2_sum__rd, alu_1_q__rd__rt, demultiplexer_1_out0,
       input_1_rdval, jump_1_reg, multiplexer_1_out, multiplexer_2_out, multiplexer_6_out, multiplexer_7_out,
       multiplexer_8_out, multiplexer_9_out, multiplexer_10_out, PC, ram_1_data, RDVAL,
       register_file_1_rs2val, RSVAL, sx_1_output_16_bit;

  Hex_Digit_Display hex_digit_display_1 (.value(PC[15:12]));  // open: dp
  Hex_Digit_Display hex_digit_display_2 (.value(register_file_1_r1_4));  // open: dp
  Hex_Digit_Display hex_digit_display_3 (.value(register_file_1_r5_4));  // open: dp
  Clock clock_1 (.out(Clk));
  Hex_Digit_Display hex_digit_display_4 (.value(PC[7:4]));  // open: dp
  Hex_Digit_Display hex_digit_display_5 (.value(PC[11:8]));  // open: dp
  Hex_Digit_Display hex_digit_display_6 (.value(register_file_1_r1_2));  // open: dp
  Hex_Digit_Display hex_digit_display_7 (.value(register_file_1_r1_3));  // open: dp
  Hex_Digit_Display hex_digit_display_8 (.value(register_file_1_r5_2));  // open: dp
  Hex_Digit_Display hex_digit_display_9 (.value(register_file_1_r5_3));  // open: dp
  Hex_Digit_Display hex_digit_display_10 (.value(PC[3:0]));  // open: dp
  Hex_Digit_Display hex_digit_display_11 (.value(register_file_1_r2_4));  // open: dp
  Hex_Digit_Display hex_digit_display_12 (.value(register_file_1_r1));  // open: dp
  Hex_Digit_Display hex_digit_display_13 (.value(register_file_1_r5));  // open: dp
  Hex_Digit_Display hex_digit_display_14 (.value(register_file_1_r6_4));  // open: dp
  register u_PC (
    .Clock_input(Clk), ._16_bit_Input(multiplexer_10_out), .Enable(1'b1), .Reset__ind_of_clock(Reset),
    ._16_bit_Output(PC));
  Hex_Digit_Display hex_digit_display_15 (.value(register_file_1_r2_3));  // open: dp
  Hex_Digit_Display hex_digit_display_16 (.value(register_file_1_r2_2));  // open: dp
  Hex_Digit_Display hex_digit_display_17 (.value(register_file_1_r6_2));  // open: dp
  Hex_Digit_Display hex_digit_display_18 (.value(register_file_1_r6_3));  // open: dp
  Hex_Digit_Display hex_digit_display_19 (.value(register_file_1_r2));  // open: dp
  Hex_Digit_Display hex_digit_display_20 (.value(register_file_1_r6));  // open: dp
  Add_Suber_16_bit add_suber_16_bit_1 (
    .a__rt(16'h1), .Cin__Add_0(1'b0), .b__rs(PC), .Sum__rd(add_suber_16_bit_1_sum__rd));  // open: Cout
  Hex_Digit_Display hex_digit_display_21 (.value(register_file_1_r3_4));  // open: dp
  Hex_Digit_Display hex_digit_display_22 (.value(register_file_1_r3_3));  // open: dp
  Hex_Digit_Display hex_digit_display_23 (.value(register_file_1_r7_4));  // open: dp
  Hex_Digit_Display hex_digit_display_24 (.value(register_file_1_r7_3));  // open: dp
  ROM #(.addrWidth(16), .dataWidth(16)) rom_1 (.addr(PC), .data({Op, Addr}));  // open: sel
  Hex_Digit_Display hex_digit_display_25 (.value(register_file_1_r3));  // open: dp
  Hex_Digit_Display hex_digit_display_26 (.value(register_file_1_r3_2));  // open: dp
  Hex_Digit_Display hex_digit_display_27 (.value(register_file_1_r7_2));  // open: dp
  Hex_Digit_Display hex_digit_display_28 (.value(register_file_1_r7));  // open: dp
  \input  input_1 (.Clk(Clk), .Reset(Reset), .RDVAL(input_1_rdval), .RW(\input ));
  Hex_Digit_Display hex_digit_display_29 (.value(register_file_1_r4_4));  // open: dp
  Hex_Digit_Display hex_digit_display_30 (.value(register_file_1_r4_3));  // open: dp
  Multiplexer #(.width(16), .enable("false")) multiplexer_1 (
    .in0(multiplexer_8_out), .in1(input_1_rdval), .out(multiplexer_1_out), .sel(\input ));
  Hex_Digit_Display hex_digit_display_31 (.value(register_file_1_r4_2));  // open: dp
  Hex_Digit_Display hex_digit_display_32 (.value(register_file_1_r4));  // open: dp
  Multiplexer #(.width(16), .enable("false")) multiplexer_2 (
    .in0(multiplexer_1_out), .in1(add_suber_16_bit_1_sum__rd), .out(multiplexer_2_out), .sel(jal));
  Multiplexer #(.width(3), .enable("false")) multiplexer_3 (
    .in0(Addr[11:9]), .in1(Addr[5:3]), .out(multiplexer_3_out), .sel(jr));
  register_file register_file_1 (
    .Clock(Clk), .RDVAL__16_bit_Input(multiplexer_2_out), .WE__Write_Enable(WE), .Reset(Reset),
    .RS2VAL(register_file_1_rs2val), .RS1VAL(RDVAL), .RD(multiplexer_5_out), .RS2(Addr[8:6]),
    .RS1(multiplexer_3_out),
    .r1({register_file_1_r1_4, register_file_1_r1_3, register_file_1_r1_2, register_file_1_r1}),
    .r2({register_file_1_r2_4, register_file_1_r2_3, register_file_1_r2_2, register_file_1_r2}),
    .r3({register_file_1_r3_4, register_file_1_r3_3, register_file_1_r3_2, register_file_1_r3}),
    .r4({register_file_1_r4_4, register_file_1_r4_3, register_file_1_r4_2, register_file_1_r4}),
    .r5({register_file_1_r5_4, register_file_1_r5_3, register_file_1_r5_2, register_file_1_r5}),
    .r6({register_file_1_r6_4, register_file_1_r6_3, register_file_1_r6_2, register_file_1_r6}),
    .r7({register_file_1_r7_4, register_file_1_r7_3, register_file_1_r7_2, register_file_1_r7}));
  Multiplexer #(.width(3), .enable("false")) multiplexer_4 (
    .in0(Addr[8:6]), .in1(Addr[5:3]), .out(multiplexer_4_out), .sel(instr_dec_1_r_type));
  Instr_Dec instr_dec_1 (
    .Opcode_4_bit(Op), .J_type(J_type), .I_type(instr_dec_1_i_type), .jal(jal), .lw(instr_dec_1_lw),
    .sw(instr_dec_1_sw), .beq(out_2), .blt(blt), .jr(jr), .input_instr(\input ), .output_instr(\output ),
    .R_type(instr_dec_1_r_type), .WE(WE));  // open: j, addi, add, sub, and, xor, sll, sra
  Demultiplexer #(.width(16), .enable("false")) demultiplexer_1 (
    .out0(demultiplexer_1_out0), .out1(RSVAL), .in(RDVAL), .sel(\output ));
  Multiplexer #(.width(3), .enable("false")) multiplexer_5 (
    .in0(multiplexer_4_out), .in1(3'b111), .out(multiplexer_5_out), .sel(jal));
  TTY #(.trigger("falling")) tty_1 (.data(RSVAL[6:0]), .clk(Clk), .clr(Reset));  // open: we
  SX sx_1 (.Input_6_bit(Addr[5:0]), .Output_16_bit(sx_1_output_16_bit));
  and and_1 (and_1_out, instr_dec_1_i_type, not_2_out, not_1_out);
  ALU alu_1 (
    .a__rt_Imm(multiplexer_6_out), .b__rs(demultiplexer_1_out0), .shamt(Addr[2:0]), .Opcode(Op),
    .Q__rd__rt(alu_1_q__rd__rt), .CoutS(Cout));  // open: CoutA
  Multiplexer #(.width(16), .enable("false")) multiplexer_6 (
    .in0(register_file_1_rs2val), .in1(sx_1_output_16_bit), .out(multiplexer_6_out), .sel(and_1_out));
  not not_1 (not_1_out, out_2);
  not not_2 (not_2_out, blt);
  Add_Suber_16_bit add_suber_16_bit_2 (
    .a__rt(add_suber_16_bit_1_sum__rd), .Cin__Add_0(1'b0), .b__rs(sx_1_output_16_bit),
    .Sum__rd(add_suber_16_bit_2_sum__rd));  // open: Cout
  and beq (beq_out, out_2, Eq_0_out);
  not not_3 (not_3_out, alu_1_q__rd__rt[11]);
  not not_4 (not_4_out, alu_1_q__rd__rt[13]);
  not not_5 (not_5_out, alu_1_q__rd__rt[14]);
  not not_6 (not_6_out, alu_1_q__rd__rt[12]);
  not not_7 (not_7_out, alu_1_q__rd__rt[9]);
  not not_8 (not_8_out, alu_1_q__rd__rt[10]);
  not not_9 (not_9_out, alu_1_q__rd__rt[15]);
  not not_10 (not_10_out, Clk);
  Multiplexer #(.width(16), .enable("false")) multiplexer_7 (
    .in0(add_suber_16_bit_1_sum__rd), .in1(add_suber_16_bit_2_sum__rd), .out(multiplexer_7_out),
    .sel(or_1_out));
  or or_1 (or_1_out, beq_out, blt_out);
  not not_11 (not_11_out, Cout);
  and Eq_0 (Eq_0_out, 1'b1, not_9_out, not_5_out, not_4_out, not_6_out, not_3_out, not_8_out, not_7_out, not_14_out, not_15_out, not_18_out, not_17_out, not_12_out, not_19_out, not_13_out, not_16_out, not_20_out);
  not not_12 (not_12_out, alu_1_q__rd__rt[4]);
  not not_13 (not_13_out, alu_1_q__rd__rt[2]);
  not not_14 (not_14_out, alu_1_q__rd__rt[8]);
  not not_15 (not_15_out, alu_1_q__rd__rt[7]);
  not not_16 (not_16_out, alu_1_q__rd__rt[1]);
  not not_17 (not_17_out, alu_1_q__rd__rt[5]);
  not not_18 (not_18_out, alu_1_q__rd__rt[6]);
  not not_19 (not_19_out, alu_1_q__rd__rt[3]);
  RAM #(.addrWidth(16), .dataWidth(16), .bus("separate")) ram_1 (
    .addr(alu_1_q__rd__rt), .din(register_file_1_rs2val), .data(ram_1_data), .str(instr_dec_1_sw),
    .clk(not_10_out), .ld(instr_dec_1_lw));  // open: sel, clr
  and u_blt (blt_out, not_11_out, blt);
  not not_20 (not_20_out, alu_1_q__rd__rt[0]);
  Multiplexer #(.width(16), .enable("false")) multiplexer_8 (
    .in0(alu_1_q__rd__rt), .in1(ram_1_data), .out(multiplexer_8_out), .sel(instr_dec_1_lw));
  Multiplexer #(.width(16), .enable("false")) multiplexer_9 (
    .in0(multiplexer_7_out), .in1(jump_1_reg), .out(multiplexer_9_out), .sel(J_type));
  jump jump_1 (.Addr(Addr), .PC(PC), .\reg (jump_1_reg));
  Multiplexer #(.width(16), .enable("false")) multiplexer_10 (
    .in0(multiplexer_9_out), .in1(RDVAL), .out(multiplexer_10_out), .sel(jr));

  // Other names for the same wires on the sheet: rt[2:0] = Addr[8:6]; rs[2:0] = Addr[11:9]; beq = out_2;
  //   Imm[5:0] = Addr[5:0]; Shamt[2:0] = Addr[2:0]; rd[2:0] = Addr[5:3]

  // Notes on the sheet:
  //   contents of rom_1 (hex, n*v repeats v):
  //   1048 520d 1240 520d 1240 5209 1240 d01d e028 1048 520d 1240 520d 1243 5209 1241 7280 2558 34a0 4528
  //   5432 6432 14be 6411 a401 410 903f 1fc1 903f 72c0 f600 1241 9601 b01d c038
  //   Data
endmodule

module Tester (
  input  [3:0] in_1,
  input  [15:0] in_2,
  input  [15:0] in_3,
  output [15:0] out_4
);

  wire clock_1_out;
  wire [6:0] keyboard_1_data;

  Controlled_Buffer controlled_buffer_1 ();  // open: in, out, en
  Clock clock_1 (.out(clock_1_out));
  Keyboard keyboard_1 (.clk(clock_1_out), .data(keyboard_1_data));  // open: re, clr, avail
  ALU alu_1 (.a__rt_Imm(in_3), .b__rs(in_2), .shamt(3'b101), .Opcode(in_1), .Q__rd__rt(out_4));  // open: CoutA, CoutS
  register register_1 (
    .Clock_input(clock_1_out), .Enable(clock_1_out));  // open: _16_bit_Input, Reset__ind_of_clock, _16_bit_Output
endmodule

module register_file (
  input  Clock,
  input  [15:0] RDVAL__16_bit_Input,
  input  WE__Write_Enable,
  input  [2:0] RS2,
  input  Reset,
  input  [2:0] RD,
  input  [2:0] RS1,
  output [15:0] RS2VAL,
  output [15:0] r1,
  output [15:0] RS1VAL,
  output [15:0] r2,
  output [15:0] r3,
  output [15:0] r4,
  output [15:0] r5,
  output [15:0] r6,
  output [15:0] r7
);

  wire decoder_1_out0, decoder_1_out1, decoder_1_out2, decoder_1_out3, decoder_1_out4, decoder_1_out5,
       decoder_1_out6, decoder_1_out7, EnT0, EnT1, EnT2, EnT3, EnT4, EnT5, EnT6, EnT7;
  wire [15:0] Register_0__16_bit_output;

  Decoder #(.select(3), .enable("false")) decoder_1 (
    .out0(decoder_1_out0), .out1(decoder_1_out1), .out2(decoder_1_out2), .out3(decoder_1_out3),
    .out4(decoder_1_out4), .out5(decoder_1_out5), .out6(decoder_1_out6), .out7(decoder_1_out7), .sel(RD));
  and and_1 (EnT0, decoder_1_out0, WE__Write_Enable);
  and and_2 (EnT1, decoder_1_out1, WE__Write_Enable);
  and and_3 (EnT2, decoder_1_out2, WE__Write_Enable);
  and and_4 (EnT3, decoder_1_out3, WE__Write_Enable);
  and and_5 (EnT4, decoder_1_out4, WE__Write_Enable);
  and and_6 (EnT5, decoder_1_out5, WE__Write_Enable);
  and and_7 (EnT6, decoder_1_out6, WE__Write_Enable);
  and and_8 (EnT7, decoder_1_out7, WE__Write_Enable);
  register Register_0 (
    .Clock_input(Clock), ._16_bit_Input({16{1'b0}}), .Enable(EnT0), .Reset__ind_of_clock(Reset),
    ._16_bit_Output(Register_0__16_bit_output));
  register Register_1 (
    .Clock_input(Clock), ._16_bit_Input(RDVAL__16_bit_Input), .Enable(EnT1), .Reset__ind_of_clock(Reset),
    ._16_bit_Output(r1));
  register Register_2 (
    .Clock_input(Clock), ._16_bit_Input(RDVAL__16_bit_Input), .Enable(EnT2), .Reset__ind_of_clock(Reset),
    ._16_bit_Output(r2));
  register Register_3 (
    .Clock_input(Clock), ._16_bit_Input(RDVAL__16_bit_Input), .Enable(EnT3), .Reset__ind_of_clock(Reset),
    ._16_bit_Output(r3));
  register Register_4 (
    .Clock_input(Clock), ._16_bit_Input(RDVAL__16_bit_Input), .Enable(EnT4), .Reset__ind_of_clock(Reset),
    ._16_bit_Output(r4));
  register Register_5 (
    .Clock_input(Clock), ._16_bit_Input(RDVAL__16_bit_Input), .Enable(EnT5), .Reset__ind_of_clock(Reset),
    ._16_bit_Output(r5));
  register Register_6 (
    .Clock_input(Clock), ._16_bit_Input(RDVAL__16_bit_Input), .Enable(EnT6), .Reset__ind_of_clock(Reset),
    ._16_bit_Output(r6));
  register Register_7 (
    .Clock_input(Clock), ._16_bit_Input(RDVAL__16_bit_Input), .Enable(EnT7), .Reset__ind_of_clock(Reset),
    ._16_bit_Output(r7));
  Multiplexer #(.select(3), .width(16), .enable("false")) multiplexer_1 (
    .in0(Register_0__16_bit_output), .in1(r1), .in2(r2), .in3(r3), .in4(r4), .in5(r5), .in6(r6), .in7(r7),
    .out(RS2VAL), .sel(RS2));
  Multiplexer #(.select(3), .width(16), .enable("false")) multiplexer_2 (
    .in0(Register_0__16_bit_output), .in1(r1), .in2(r2), .in3(r3), .in4(r4), .in5(r5), .in6(r6), .in7(r7),
    .out(RS1VAL), .sel(RS1));

  // Other names for the same wires on the sheet: _16InT[15:0] = RDVAL__16_bit_Input; ClkT = Clock; ResetT = Reset
endmodule

module register (
  input  Clock_input,
  input  [15:0] _16_bit_Input,
  input  Enable,
  input  Reset__ind_of_clock,
  output [15:0] _16_bit_Output
);

  D_Flip_Flop #(.trigger("falling")) d_ff_1 (
    .clk(Clock_input), .D(_16_bit_Input[0]), .Q(_16_bit_Output[0]), .en(Enable), .reset(Reset__ind_of_clock));  // open: Qn, preset
  D_Flip_Flop #(.trigger("falling")) d_ff_2 (
    .clk(Clock_input), .D(_16_bit_Input[1]), .Q(_16_bit_Output[1]), .en(Enable), .reset(Reset__ind_of_clock));  // open: Qn, preset
  D_Flip_Flop #(.trigger("falling")) d_ff_3 (
    .clk(Clock_input), .D(_16_bit_Input[2]), .Q(_16_bit_Output[2]), .en(Enable), .reset(Reset__ind_of_clock));  // open: Qn, preset
  D_Flip_Flop #(.trigger("falling")) d_ff_4 (
    .clk(Clock_input), .D(_16_bit_Input[3]), .Q(_16_bit_Output[3]), .en(Enable), .reset(Reset__ind_of_clock));  // open: Qn, preset
  D_Flip_Flop #(.trigger("falling")) d_ff_5 (
    .clk(Clock_input), .D(_16_bit_Input[4]), .Q(_16_bit_Output[4]), .en(Enable), .reset(Reset__ind_of_clock));  // open: Qn, preset
  D_Flip_Flop #(.trigger("falling")) d_ff_6 (
    .clk(Clock_input), .D(_16_bit_Input[5]), .Q(_16_bit_Output[5]), .en(Enable), .reset(Reset__ind_of_clock));  // open: Qn, preset
  D_Flip_Flop #(.trigger("falling")) d_ff_7 (
    .clk(Clock_input), .D(_16_bit_Input[6]), .Q(_16_bit_Output[6]), .en(Enable), .reset(Reset__ind_of_clock));  // open: Qn, preset
  D_Flip_Flop #(.trigger("falling")) d_ff_8 (
    .clk(Clock_input), .D(_16_bit_Input[7]), .Q(_16_bit_Output[7]), .en(Enable), .reset(Reset__ind_of_clock));  // open: Qn, preset
  D_Flip_Flop #(.trigger("falling")) d_ff_9 (
    .clk(Clock_input), .D(_16_bit_Input[8]), .Q(_16_bit_Output[8]), .en(Enable), .reset(Reset__ind_of_clock));  // open: Qn, preset
  D_Flip_Flop #(.trigger("falling")) d_ff_10 (
    .clk(Clock_input), .D(_16_bit_Input[9]), .Q(_16_bit_Output[9]), .en(Enable), .reset(Reset__ind_of_clock));  // open: Qn, preset
  D_Flip_Flop #(.trigger("falling")) d_ff_11 (
    .clk(Clock_input), .D(_16_bit_Input[10]), .Q(_16_bit_Output[10]), .en(Enable), .reset(Reset__ind_of_clock));  // open: Qn, preset
  D_Flip_Flop #(.trigger("falling")) d_ff_12 (
    .clk(Clock_input), .D(_16_bit_Input[11]), .Q(_16_bit_Output[11]), .en(Enable), .reset(Reset__ind_of_clock));  // open: Qn, preset
  D_Flip_Flop #(.trigger("falling")) d_ff_13 (
    .clk(Clock_input), .D(_16_bit_Input[12]), .Q(_16_bit_Output[12]), .en(Enable), .reset(Reset__ind_of_clock));  // open: Qn, preset
  D_Flip_Flop #(.trigger("falling")) d_ff_14 (
    .clk(Clock_input), .D(_16_bit_Input[13]), .Q(_16_bit_Output[13]), .en(Enable), .reset(Reset__ind_of_clock));  // open: Qn, preset
  D_Flip_Flop #(.trigger("falling")) d_ff_15 (
    .clk(Clock_input), .D(_16_bit_Input[14]), .Q(_16_bit_Output[14]), .en(Enable), .reset(Reset__ind_of_clock));  // open: Qn, preset
  D_Flip_Flop #(.trigger("falling")) d_ff_16 (
    .clk(Clock_input), .D(_16_bit_Input[15]), .Q(_16_bit_Output[15]), .en(Enable), .reset(Reset__ind_of_clock));  // open: Qn, preset
endmodule

module ALU (
  input  [15:0] a__rt_Imm,
  input  [3:0] Opcode,
  input  [15:0] b__rs,
  input  [2:0] shamt,
  output CoutA,
  output [15:0] Q__rd__rt,
  output CoutS
);

  wire [15:0] add_sum__rd, And__0_011_out, sll_1_rd, sra_1_rd, sub_sum__rd, Xor__0_100_out;

  Add_Suber_16_bit add (.a__rt(a__rt_Imm), .Cin__Add_0(1'b0), .b__rs(b__rs), .Sum__rd(add_sum__rd), .Cout(CoutA));
  Add_Suber_16_bit sub (.a__rt(a__rt_Imm), .Cin__Add_0(1'b1), .b__rs(b__rs), .Sum__rd(sub_sum__rd), .Cout(CoutS));
  assign And__0_011_out = a__rt_Imm & b__rs;  // AND_Gate And__0_011, 16 bits wide
  assign Xor__0_100_out = a__rt_Imm ^ b__rs;  // XOR_Gate Xor__0_100, 16 bits wide
  SLL sll_1 (.rs(b__rs), .shamt(shamt), .rd(sll_1_rd));
  SRA sra_1 (.rs(b__rs), .shamt(shamt), .rd(sra_1_rd));
  Multiplexer #(.select(4), .width(16), .enable("false")) multiplexer_1 (
    .in0(add_sum__rd), .in1(add_sum__rd), .in2(sub_sum__rd), .in3(And__0_011_out), .in4(Xor__0_100_out),
    .in5(sll_1_rd), .in6(sra_1_rd), .in7(add_sum__rd), .in8(add_sum__rd), .in9(sub_sum__rd),
    .in10(sub_sum__rd), .in11(add_sum__rd), .in12(b__rs), .in13(add_sum__rd), .in14(add_sum__rd),
    .in15(add_sum__rd), .out(Q__rd__rt), .sel(Opcode));

  // Other names for the same wires on the sheet: a[15:0] = a__rt_Imm; b[15:0] = b__rs

  // Notes on the sheet:
  //   Addi -> write to $rt
endmodule

module Add_Suber_16_bit (
  input  [15:0] a__rt,
  input  Cin__Add_0,
  input  [15:0] b__rs,
  output [15:0] Sum__rd,
  output Cout
);

  wire bit_0_cout, bit_1_cout, bit_2_cout, bit_3_cout, bit_4_cout, bit_5_cout, bit_6_cout, bit_7_cout,
       bit_8_cout, bit_9_cout, bit_10_cout, bit_11_cout, bit_12_cout, bit_13_cout, bit_14_cout, xor_1_out,
       xor_2_out, xor_3_out, xor_4_out, xor_5_out, xor_6_out, xor_7_out, xor_8_out, xor_9_out, xor_10_out,
       xor_11_out, xor_12_out, xor_13_out, xor_14_out, xor_15_out, xor_16_out;

  Adder_1_bit bit_0 (.a(xor_1_out), .b(b__rs[0]), .Cin(Cin__Add_0), .Cout(bit_0_cout), .Sum(Sum__rd[0]));
  xor xor_1 (xor_1_out, Cin__Add_0, a__rt[0]);
  Adder_1_bit bit_8 (.a(xor_2_out), .b(b__rs[8]), .Cin(bit_7_cout), .Cout(bit_8_cout), .Sum(Sum__rd[8]));
  xor xor_2 (xor_2_out, Cin__Add_0, a__rt[8]);
  Adder_1_bit bit_1 (.a(xor_3_out), .b(b__rs[1]), .Cin(bit_0_cout), .Cout(bit_1_cout), .Sum(Sum__rd[1]));
  xor xor_3 (xor_3_out, Cin__Add_0, a__rt[1]);
  Adder_1_bit bit_9 (.a(xor_4_out), .b(b__rs[9]), .Cin(bit_8_cout), .Cout(bit_9_cout), .Sum(Sum__rd[9]));
  xor xor_4 (xor_4_out, Cin__Add_0, a__rt[9]);
  Adder_1_bit bit_2 (.a(xor_5_out), .b(b__rs[2]), .Cin(bit_1_cout), .Cout(bit_2_cout), .Sum(Sum__rd[2]));
  xor xor_5 (xor_5_out, Cin__Add_0, a__rt[2]);
  Adder_1_bit bit_10 (.a(xor_6_out), .b(b__rs[10]), .Cin(bit_9_cout), .Cout(bit_10_cout), .Sum(Sum__rd[10]));
  xor xor_6 (xor_6_out, Cin__Add_0, a__rt[10]);
  Adder_1_bit bit_3 (.a(xor_7_out), .b(b__rs[3]), .Cin(bit_2_cout), .Cout(bit_3_cout), .Sum(Sum__rd[3]));
  xor xor_7 (xor_7_out, Cin__Add_0, a__rt[3]);
  Adder_1_bit bit_11 (.a(xor_8_out), .b(b__rs[11]), .Cin(bit_10_cout), .Cout(bit_11_cout), .Sum(Sum__rd[11]));
  xor xor_8 (xor_8_out, Cin__Add_0, a__rt[11]);
  xor xor_9 (xor_9_out, Cin__Add_0, a__rt[4]);
  xor xor_10 (xor_10_out, Cin__Add_0, a__rt[12]);
  Adder_1_bit bit_4 (.a(xor_9_out), .b(b__rs[4]), .Cin(bit_3_cout), .Cout(bit_4_cout), .Sum(Sum__rd[4]));
  Adder_1_bit bit_12 (.a(xor_10_out), .b(b__rs[12]), .Cin(bit_11_cout), .Cout(bit_12_cout), .Sum(Sum__rd[12]));
  Adder_1_bit bit_5 (.a(xor_11_out), .b(b__rs[5]), .Cin(bit_4_cout), .Cout(bit_5_cout), .Sum(Sum__rd[5]));
  xor xor_11 (xor_11_out, Cin__Add_0, a__rt[5]);
  Adder_1_bit bit_13 (.a(xor_12_out), .b(b__rs[13]), .Cin(bit_12_cout), .Cout(bit_13_cout), .Sum(Sum__rd[13]));
  xor xor_12 (xor_12_out, Cin__Add_0, a__rt[13]);
  Adder_1_bit bit_6 (.a(xor_13_out), .b(b__rs[6]), .Cin(bit_5_cout), .Cout(bit_6_cout), .Sum(Sum__rd[6]));
  xor xor_13 (xor_13_out, Cin__Add_0, a__rt[6]);
  Adder_1_bit bit_14 (.a(xor_14_out), .b(b__rs[14]), .Cin(bit_13_cout), .Cout(bit_14_cout), .Sum(Sum__rd[14]));
  xor xor_14 (xor_14_out, Cin__Add_0, a__rt[14]);
  xor xor_15 (xor_15_out, Cin__Add_0, a__rt[7]);
  xor xor_16 (xor_16_out, Cin__Add_0, a__rt[15]);
  Adder_1_bit bit_7 (.a(xor_15_out), .b(b__rs[7]), .Cin(bit_6_cout), .Cout(bit_7_cout), .Sum(Sum__rd[7]));
  Adder_1_bit bit_15 (.a(xor_16_out), .b(b__rs[15]), .Cin(bit_14_cout), .Cout(Cout), .Sum(Sum__rd[15]));

  // Other names for the same wires on the sheet: a0_7[7:0] = a__rt[7:0]; a8_15[7:0] = a__rt[15:8];
  //   b0_7[7:0] = b__rs[7:0]; b8_15[7:0] = b__rs[15:8]; Sum0_7[7:0] = Sum__rd[7:0]; Sum8_15[7:0] = Sum__rd[15:8]
endmodule

module Adder_1_bit (
  input  Cin,
  input  a,
  input  b,
  output Sum,
  output Cout
);

  wire and_1_out, and_2_out, xor_1_out;

  and and_1 (and_1_out, b, a);
  xor xor_1 (xor_1_out, a, b);
  or or_1 (Cout, and_1_out, and_2_out);
  and and_2 (and_2_out, xor_1_out, Cin);
  xor xor_2 (Sum, Cin, xor_1_out);
endmodule

module SLL (
  input  [15:0] rs,
  input  [2:0] shamt,
  output [15:0] rd
);

  wire multiplexer_1_out, multiplexer_2_out, multiplexer_3_out, multiplexer_4_out, multiplexer_5_out,
       multiplexer_6_out, multiplexer_7_out, multiplexer_8_out, multiplexer_9_out, multiplexer_10_out,
       multiplexer_11_out, multiplexer_12_out, multiplexer_13_out, multiplexer_14_out, multiplexer_15_out,
       multiplexer_16_out, multiplexer_17_out, multiplexer_18_out, multiplexer_19_out, multiplexer_20_out,
       multiplexer_21_out, multiplexer_22_out, multiplexer_23_out, multiplexer_24_out, multiplexer_25_out,
       multiplexer_26_out, multiplexer_27_out, multiplexer_28_out, multiplexer_29_out, multiplexer_30_out,
       multiplexer_31_out, multiplexer_32_out;

  Multiplexer #(.enable("false")) multiplexer_1 (.in0(rs[15]), .in1(rs[14]), .out(multiplexer_1_out), .sel(shamt[0]));
  Multiplexer #(.enable("false")) multiplexer_2 (.in0(rs[14]), .in1(rs[13]), .out(multiplexer_2_out), .sel(shamt[0]));
  Multiplexer #(.enable("false")) multiplexer_3 (.in0(rs[13]), .in1(rs[12]), .out(multiplexer_3_out), .sel(shamt[0]));
  Multiplexer #(.enable("false")) multiplexer_4 (.in0(rs[12]), .in1(rs[11]), .out(multiplexer_4_out), .sel(shamt[0]));
  Multiplexer #(.enable("false")) multiplexer_5 (.in0(rs[11]), .in1(rs[10]), .out(multiplexer_5_out), .sel(shamt[0]));
  Multiplexer #(.enable("false")) multiplexer_6 (.in0(rs[10]), .in1(rs[9]), .out(multiplexer_6_out), .sel(shamt[0]));
  Multiplexer #(.enable("false")) multiplexer_7 (.in0(rs[9]), .in1(rs[8]), .out(multiplexer_7_out), .sel(shamt[0]));
  Multiplexer #(.enable("false")) multiplexer_8 (.in0(rs[8]), .in1(rs[7]), .out(multiplexer_8_out), .sel(shamt[0]));
  Multiplexer #(.enable("false")) multiplexer_9 (.in0(rs[7]), .in1(rs[6]), .out(multiplexer_9_out), .sel(shamt[0]));
  Multiplexer #(.enable("false")) multiplexer_10 (.in0(rs[6]), .in1(rs[5]), .out(multiplexer_10_out), .sel(shamt[0]));
  Multiplexer #(.enable("false")) multiplexer_11 (.in0(rs[5]), .in1(rs[4]), .out(multiplexer_11_out), .sel(shamt[0]));
  Multiplexer #(.enable("false")) multiplexer_12 (.in0(rs[4]), .in1(rs[3]), .out(multiplexer_12_out), .sel(shamt[0]));
  Multiplexer #(.enable("false")) multiplexer_13 (.in0(rs[3]), .in1(rs[2]), .out(multiplexer_13_out), .sel(shamt[0]));
  Multiplexer #(.enable("false")) multiplexer_14 (.in0(rs[2]), .in1(rs[1]), .out(multiplexer_14_out), .sel(shamt[0]));
  Multiplexer #(.enable("false")) multiplexer_15 (.in0(rs[1]), .in1(rs[0]), .out(multiplexer_15_out), .sel(shamt[0]));
  Multiplexer #(.enable("false")) multiplexer_16 (.in0(rs[0]), .in1(1'b0), .out(multiplexer_16_out), .sel(shamt[0]));
  Multiplexer #(.enable("false")) multiplexer_17 (
    .in0(multiplexer_1_out), .in1(multiplexer_3_out), .out(multiplexer_17_out), .sel(shamt[1]));
  Multiplexer #(.enable("false")) multiplexer_18 (
    .in0(multiplexer_2_out), .in1(multiplexer_4_out), .out(multiplexer_18_out), .sel(shamt[1]));
  Multiplexer #(.enable("false")) multiplexer_19 (
    .in0(multiplexer_3_out), .in1(multiplexer_5_out), .out(multiplexer_19_out), .sel(shamt[1]));
  Multiplexer #(.enable("false")) multiplexer_20 (
    .in0(multiplexer_4_out), .in1(multiplexer_6_out), .out(multiplexer_20_out), .sel(shamt[1]));
  Multiplexer #(.enable("false")) multiplexer_21 (
    .in0(multiplexer_5_out), .in1(multiplexer_7_out), .out(multiplexer_21_out), .sel(shamt[1]));
  Multiplexer #(.enable("false")) multiplexer_22 (
    .in0(multiplexer_6_out), .in1(multiplexer_8_out), .out(multiplexer_22_out), .sel(shamt[1]));
  Multiplexer #(.enable("false")) multiplexer_23 (
    .in0(multiplexer_7_out), .in1(multiplexer_9_out), .out(multiplexer_23_out), .sel(shamt[1]));
  Multiplexer #(.enable("false")) multiplexer_24 (
    .in0(multiplexer_8_out), .in1(multiplexer_10_out), .out(multiplexer_24_out), .sel(shamt[1]));
  Multiplexer #(.enable("false")) multiplexer_25 (
    .in0(multiplexer_9_out), .in1(multiplexer_11_out), .out(multiplexer_25_out), .sel(shamt[1]));
  Multiplexer #(.enable("false")) multiplexer_26 (
    .in0(multiplexer_10_out), .in1(multiplexer_12_out), .out(multiplexer_26_out), .sel(shamt[1]));
  Multiplexer #(.enable("false")) multiplexer_27 (
    .in0(multiplexer_11_out), .in1(multiplexer_13_out), .out(multiplexer_27_out), .sel(shamt[1]));
  Multiplexer #(.enable("false")) multiplexer_28 (
    .in0(multiplexer_12_out), .in1(multiplexer_14_out), .out(multiplexer_28_out), .sel(shamt[1]));
  Multiplexer #(.enable("false")) multiplexer_29 (
    .in0(multiplexer_13_out), .in1(multiplexer_15_out), .out(multiplexer_29_out), .sel(shamt[1]));
  Multiplexer #(.enable("false")) multiplexer_30 (
    .in0(multiplexer_14_out), .in1(multiplexer_16_out), .out(multiplexer_30_out), .sel(shamt[1]));
  Multiplexer #(.enable("false")) multiplexer_31 (
    .in0(multiplexer_15_out), .in1(1'b0), .out(multiplexer_31_out), .sel(shamt[1]));
  Multiplexer #(.enable("false")) multiplexer_32 (
    .in0(multiplexer_16_out), .in1(1'b0), .out(multiplexer_32_out), .sel(shamt[1]));
  Multiplexer #(.enable("false")) multiplexer_33 (
    .in0(multiplexer_17_out), .in1(multiplexer_21_out), .out(rd[15]), .sel(shamt[2]));
  Multiplexer #(.enable("false")) multiplexer_34 (
    .in0(multiplexer_18_out), .in1(multiplexer_22_out), .out(rd[14]), .sel(shamt[2]));
  Multiplexer #(.enable("false")) multiplexer_35 (
    .in0(multiplexer_19_out), .in1(multiplexer_23_out), .out(rd[13]), .sel(shamt[2]));
  Multiplexer #(.enable("false")) multiplexer_36 (
    .in0(multiplexer_20_out), .in1(multiplexer_24_out), .out(rd[12]), .sel(shamt[2]));
  Multiplexer #(.enable("false")) multiplexer_37 (
    .in0(multiplexer_21_out), .in1(multiplexer_25_out), .out(rd[11]), .sel(shamt[2]));
  Multiplexer #(.enable("false")) multiplexer_38 (
    .in0(multiplexer_22_out), .in1(multiplexer_26_out), .out(rd[10]), .sel(shamt[2]));
  Multiplexer #(.enable("false")) multiplexer_39 (
    .in0(multiplexer_23_out), .in1(multiplexer_27_out), .out(rd[9]), .sel(shamt[2]));
  Multiplexer #(.enable("false")) multiplexer_40 (
    .in0(multiplexer_24_out), .in1(multiplexer_28_out), .out(rd[8]), .sel(shamt[2]));
  Multiplexer #(.enable("false")) multiplexer_41 (
    .in0(multiplexer_25_out), .in1(multiplexer_29_out), .out(rd[7]), .sel(shamt[2]));
  Multiplexer #(.enable("false")) multiplexer_42 (
    .in0(multiplexer_26_out), .in1(multiplexer_30_out), .out(rd[6]), .sel(shamt[2]));
  Multiplexer #(.enable("false")) multiplexer_43 (
    .in0(multiplexer_27_out), .in1(multiplexer_31_out), .out(rd[5]), .sel(shamt[2]));
  Multiplexer #(.enable("false")) multiplexer_44 (
    .in0(multiplexer_28_out), .in1(multiplexer_32_out), .out(rd[4]), .sel(shamt[2]));
  Multiplexer #(.enable("false")) multiplexer_45 (.in0(multiplexer_29_out), .in1(1'b0), .out(rd[3]), .sel(shamt[2]));
  Multiplexer #(.enable("false")) multiplexer_46 (.in0(multiplexer_30_out), .in1(1'b0), .out(rd[2]), .sel(shamt[2]));
  Multiplexer #(.enable("false")) multiplexer_47 (.in0(multiplexer_31_out), .in1(1'b0), .out(rd[1]), .sel(shamt[2]));
  Multiplexer #(.enable("false")) multiplexer_48 (.in0(multiplexer_32_out), .in1(1'b0), .out(rd[0]), .sel(shamt[2]));
endmodule

module SRA (
  input  [15:0] rs,
  input  [2:0] shamt,
  output [15:0] rd
);

  wire multiplexer_1_out, multiplexer_2_out, multiplexer_3_out, multiplexer_4_out, multiplexer_5_out,
       multiplexer_6_out, multiplexer_7_out, multiplexer_8_out, multiplexer_9_out, multiplexer_10_out,
       multiplexer_11_out, multiplexer_12_out, multiplexer_13_out, multiplexer_14_out, multiplexer_15_out,
       multiplexer_16_out, multiplexer_17_out, multiplexer_18_out, multiplexer_19_out, multiplexer_20_out,
       multiplexer_21_out, multiplexer_22_out, multiplexer_23_out, multiplexer_24_out, multiplexer_25_out,
       multiplexer_26_out, multiplexer_27_out, multiplexer_28_out, multiplexer_29_out, multiplexer_30_out,
       multiplexer_31_out, multiplexer_32_out;

  Multiplexer #(.enable("false")) multiplexer_1 (.in0(rs[0]), .in1(rs[1]), .out(multiplexer_1_out), .sel(shamt[0]));
  Multiplexer #(.enable("false")) multiplexer_2 (.in0(rs[1]), .in1(rs[2]), .out(multiplexer_2_out), .sel(shamt[0]));
  Multiplexer #(.enable("false")) multiplexer_3 (.in0(rs[2]), .in1(rs[3]), .out(multiplexer_3_out), .sel(shamt[0]));
  Multiplexer #(.enable("false")) multiplexer_4 (.in0(rs[3]), .in1(rs[4]), .out(multiplexer_4_out), .sel(shamt[0]));
  Multiplexer #(.enable("false")) multiplexer_5 (.in0(rs[4]), .in1(rs[5]), .out(multiplexer_5_out), .sel(shamt[0]));
  Multiplexer #(.enable("false")) multiplexer_6 (.in0(rs[5]), .in1(rs[6]), .out(multiplexer_6_out), .sel(shamt[0]));
  Multiplexer #(.enable("false")) multiplexer_7 (.in0(rs[6]), .in1(rs[7]), .out(multiplexer_7_out), .sel(shamt[0]));
  Multiplexer #(.enable("false")) multiplexer_8 (.in0(rs[7]), .in1(rs[8]), .out(multiplexer_8_out), .sel(shamt[0]));
  Multiplexer #(.enable("false")) multiplexer_9 (.in0(rs[8]), .in1(rs[9]), .out(multiplexer_9_out), .sel(shamt[0]));
  Multiplexer #(.enable("false")) multiplexer_10 (.in0(rs[9]), .in1(rs[10]), .out(multiplexer_10_out), .sel(shamt[0]));
  Multiplexer #(.enable("false")) multiplexer_11 (.in0(rs[10]), .in1(rs[11]), .out(multiplexer_11_out), .sel(shamt[0]));
  Multiplexer #(.enable("false")) multiplexer_12 (.in0(rs[11]), .in1(rs[12]), .out(multiplexer_12_out), .sel(shamt[0]));
  Multiplexer #(.enable("false")) multiplexer_13 (.in0(rs[12]), .in1(rs[13]), .out(multiplexer_13_out), .sel(shamt[0]));
  Multiplexer #(.enable("false")) multiplexer_14 (.in0(rs[13]), .in1(rs[14]), .out(multiplexer_14_out), .sel(shamt[0]));
  Multiplexer #(.enable("false")) multiplexer_15 (.in0(rs[14]), .in1(rs[15]), .out(multiplexer_15_out), .sel(shamt[0]));
  Multiplexer #(.enable("false")) multiplexer_16 (.in0(rs[15]), .in1(rs[15]), .out(multiplexer_16_out), .sel(shamt[0]));
  Multiplexer #(.enable("false")) multiplexer_17 (
    .in0(multiplexer_1_out), .in1(multiplexer_3_out), .out(multiplexer_17_out), .sel(shamt[1]));
  Multiplexer #(.enable("false")) multiplexer_18 (
    .in0(multiplexer_2_out), .in1(multiplexer_4_out), .out(multiplexer_18_out), .sel(shamt[1]));
  Multiplexer #(.enable("false")) multiplexer_19 (
    .in0(multiplexer_3_out), .in1(multiplexer_5_out), .out(multiplexer_19_out), .sel(shamt[1]));
  Multiplexer #(.enable("false")) multiplexer_20 (
    .in0(multiplexer_4_out), .in1(multiplexer_6_out), .out(multiplexer_20_out), .sel(shamt[1]));
  Multiplexer #(.enable("false")) multiplexer_21 (
    .in0(multiplexer_5_out), .in1(multiplexer_7_out), .out(multiplexer_21_out), .sel(shamt[1]));
  Multiplexer #(.enable("false")) multiplexer_22 (
    .in0(multiplexer_6_out), .in1(multiplexer_8_out), .out(multiplexer_22_out), .sel(shamt[1]));
  Multiplexer #(.enable("false")) multiplexer_23 (
    .in0(multiplexer_7_out), .in1(multiplexer_9_out), .out(multiplexer_23_out), .sel(shamt[1]));
  Multiplexer #(.enable("false")) multiplexer_24 (
    .in0(multiplexer_8_out), .in1(multiplexer_10_out), .out(multiplexer_24_out), .sel(shamt[1]));
  Multiplexer #(.enable("false")) multiplexer_25 (
    .in0(multiplexer_9_out), .in1(multiplexer_11_out), .out(multiplexer_25_out), .sel(shamt[1]));
  Multiplexer #(.enable("false")) multiplexer_26 (
    .in0(multiplexer_10_out), .in1(multiplexer_12_out), .out(multiplexer_26_out), .sel(shamt[1]));
  Multiplexer #(.enable("false")) multiplexer_27 (
    .in0(multiplexer_11_out), .in1(multiplexer_13_out), .out(multiplexer_27_out), .sel(shamt[1]));
  Multiplexer #(.enable("false")) multiplexer_28 (
    .in0(multiplexer_12_out), .in1(multiplexer_14_out), .out(multiplexer_28_out), .sel(shamt[1]));
  Multiplexer #(.enable("false")) multiplexer_29 (
    .in0(multiplexer_13_out), .in1(multiplexer_15_out), .out(multiplexer_29_out), .sel(shamt[1]));
  Multiplexer #(.enable("false")) multiplexer_30 (
    .in0(multiplexer_14_out), .in1(multiplexer_16_out), .out(multiplexer_30_out), .sel(shamt[1]));
  Multiplexer #(.enable("false")) multiplexer_31 (
    .in0(multiplexer_15_out), .in1(rs[15]), .out(multiplexer_31_out), .sel(shamt[1]));
  Multiplexer #(.enable("false")) multiplexer_32 (
    .in0(multiplexer_16_out), .in1(rs[15]), .out(multiplexer_32_out), .sel(shamt[1]));
  Multiplexer #(.enable("false")) multiplexer_33 (
    .in0(multiplexer_17_out), .in1(multiplexer_21_out), .out(rd[0]), .sel(shamt[2]));
  Multiplexer #(.enable("false")) multiplexer_34 (
    .in0(multiplexer_18_out), .in1(multiplexer_22_out), .out(rd[1]), .sel(shamt[2]));
  Multiplexer #(.enable("false")) multiplexer_35 (
    .in0(multiplexer_19_out), .in1(multiplexer_23_out), .out(rd[2]), .sel(shamt[2]));
  Multiplexer #(.enable("false")) multiplexer_36 (
    .in0(multiplexer_20_out), .in1(multiplexer_24_out), .out(rd[3]), .sel(shamt[2]));
  Multiplexer #(.enable("false")) multiplexer_37 (
    .in0(multiplexer_21_out), .in1(multiplexer_25_out), .out(rd[4]), .sel(shamt[2]));
  Multiplexer #(.enable("false")) multiplexer_38 (
    .in0(multiplexer_22_out), .in1(multiplexer_26_out), .out(rd[5]), .sel(shamt[2]));
  Multiplexer #(.enable("false")) multiplexer_39 (
    .in0(multiplexer_23_out), .in1(multiplexer_27_out), .out(rd[6]), .sel(shamt[2]));
  Multiplexer #(.enable("false")) multiplexer_40 (
    .in0(multiplexer_24_out), .in1(multiplexer_28_out), .out(rd[7]), .sel(shamt[2]));
  Multiplexer #(.enable("false")) multiplexer_41 (
    .in0(multiplexer_25_out), .in1(multiplexer_29_out), .out(rd[8]), .sel(shamt[2]));
  Multiplexer #(.enable("false")) multiplexer_42 (
    .in0(multiplexer_26_out), .in1(multiplexer_30_out), .out(rd[9]), .sel(shamt[2]));
  Multiplexer #(.enable("false")) multiplexer_43 (
    .in0(multiplexer_27_out), .in1(multiplexer_31_out), .out(rd[10]), .sel(shamt[2]));
  Multiplexer #(.enable("false")) multiplexer_44 (
    .in0(multiplexer_28_out), .in1(multiplexer_32_out), .out(rd[11]), .sel(shamt[2]));
  Multiplexer #(.enable("false")) multiplexer_45 (.in0(multiplexer_29_out), .in1(rs[15]), .out(rd[12]), .sel(shamt[2]));
  Multiplexer #(.enable("false")) multiplexer_46 (.in0(multiplexer_30_out), .in1(rs[15]), .out(rd[13]), .sel(shamt[2]));
  Multiplexer #(.enable("false")) multiplexer_47 (.in0(multiplexer_31_out), .in1(rs[15]), .out(rd[14]), .sel(shamt[2]));
  Multiplexer #(.enable("false")) multiplexer_48 (.in0(multiplexer_32_out), .in1(rs[15]), .out(rd[15]), .sel(shamt[2]));
endmodule

module SX (
  input  [5:0] Input_6_bit,
  output [15:0] Output_16_bit
);


  assign Output_16_bit = {{11{Input_6_bit[5]}}, Input_6_bit[4:0]};
endmodule

module Instr_Dec (
  input  [3:0] Opcode_4_bit,
  output add,
  output j,
  output J_type,
  output sub,
  output jal,
  output \and ,
  output addi,
  output \xor ,
  output lw,
  output sll,
  output R_type,
  output sw,
  output I_type,
  output sra,
  output beq,
  output jr,
  output blt,
  output input_instr,
  output output_instr,
  output WE
);

  wire not_1_out, not_2_out, not_3_out, not_4_out, not_5_out, not_6_out, not_7_out, not_8_out, not_9_out,
       not_10_out, not_11_out, not_12_out, not_13_out, not_14_out, not_15_out, not_16_out, not_17_out,
       not_18_out, not_19_out, not_20_out, not_21_out, not_22_out, not_23_out, not_24_out, not_25_out,
       not_26_out, not_27_out, not_28_out, not_29_out, not_30_out, not_31_out, not_32_out;

  not not_1 (not_1_out, Opcode_4_bit[2]);
  not not_2 (not_2_out, Opcode_4_bit[1]);
  not not_3 (not_3_out, Opcode_4_bit[3]);
  not not_4 (not_4_out, Opcode_4_bit[2]);
  not not_5 (not_5_out, Opcode_4_bit[1]);
  not not_6 (not_6_out, Opcode_4_bit[3]);
  not not_7 (not_7_out, Opcode_4_bit[2]);
  not not_8 (not_8_out, Opcode_4_bit[1]);
  not not_9 (not_9_out, Opcode_4_bit[0]);
  not not_10 (not_10_out, Opcode_4_bit[2]);
  not not_11 (not_11_out, Opcode_4_bit[1]);
  not not_12 (not_12_out, Opcode_4_bit[2]);
  not not_13 (not_13_out, Opcode_4_bit[0]);
  and j_1011 (j, Opcode_4_bit[3], not_1_out, Opcode_4_bit[1], Opcode_4_bit[0]);
  and jal_1101 (jal, Opcode_4_bit[3], Opcode_4_bit[2], not_2_out, Opcode_4_bit[0]);
  and addi_0001 (addi, not_3_out, not_4_out, not_5_out, Opcode_4_bit[0]);
  and lw_0111 (lw, not_6_out, Opcode_4_bit[2], Opcode_4_bit[1], Opcode_4_bit[0]);
  and sw_1000 (sw, Opcode_4_bit[3], not_7_out, not_8_out, not_9_out);
  and beq_1001 (beq, Opcode_4_bit[3], not_10_out, not_11_out, Opcode_4_bit[0]);
  and blt_1010 (blt, Opcode_4_bit[3], not_12_out, Opcode_4_bit[1], not_13_out);
  or or_1 (WE, add, addi, sub, \and , \xor , sll, sra, input_instr, lw, jal);
  or u_J_type (J_type, j, jal);
  or u_I_type (I_type, addi, lw, sw, beq, blt);
  not not_14 (not_14_out, Opcode_4_bit[3]);
  not not_15 (not_15_out, Opcode_4_bit[2]);
  not not_16 (not_16_out, Opcode_4_bit[1]);
  not not_17 (not_17_out, Opcode_4_bit[0]);
  not not_18 (not_18_out, Opcode_4_bit[3]);
  not not_19 (not_19_out, Opcode_4_bit[2]);
  not not_20 (not_20_out, Opcode_4_bit[0]);
  not not_21 (not_21_out, Opcode_4_bit[3]);
  not not_22 (not_22_out, Opcode_4_bit[2]);
  not not_23 (not_23_out, Opcode_4_bit[3]);
  not not_24 (not_24_out, Opcode_4_bit[1]);
  not not_25 (not_25_out, Opcode_4_bit[0]);
  not not_26 (not_26_out, Opcode_4_bit[3]);
  not not_27 (not_27_out, Opcode_4_bit[1]);
  not not_28 (not_28_out, Opcode_4_bit[3]);
  not not_29 (not_29_out, Opcode_4_bit[0]);
  not not_30 (not_30_out, Opcode_4_bit[1]);
  not not_31 (not_31_out, Opcode_4_bit[0]);
  not not_32 (not_32_out, Opcode_4_bit[0]);
  and add_0000 (add, not_14_out, not_15_out, not_16_out, not_17_out);
  and sub_0010 (sub, not_18_out, not_19_out, Opcode_4_bit[1], not_20_out);
  and and_0011 (\and , not_21_out, not_22_out, Opcode_4_bit[1], Opcode_4_bit[0]);
  and xor_0100 (\xor , not_23_out, Opcode_4_bit[2], not_24_out, not_25_out);
  and sll_0101 (sll, not_26_out, Opcode_4_bit[2], not_27_out, Opcode_4_bit[0]);
  and sra_0110 (sra, not_28_out, Opcode_4_bit[2], Opcode_4_bit[1], not_29_out);
  and jr_1100 (jr, Opcode_4_bit[3], Opcode_4_bit[2], not_30_out, not_31_out);
  and input_1110 (input_instr, Opcode_4_bit[3], Opcode_4_bit[2], Opcode_4_bit[1], not_32_out);
  and output_1111 (output_instr, Opcode_4_bit[3], Opcode_4_bit[2], Opcode_4_bit[1], Opcode_4_bit[0]);
  or u_R_type (R_type, add, sub, \and , \xor , sll, sra, jr, input_instr, output_instr);

  // Other names for the same wires on the sheet: input = input_instr; output = output_instr
endmodule

module jump (
  input  [11:0] Addr,
  input  [15:0] PC,
  output [15:0] \reg 
);


  assign \reg  = {PC[15:12], Addr};
endmodule

module \input  (
  input  Clk,
  input  RW,
  input  Reset,
  output [15:0] RDVAL
);

  wire keyboard_1_avail, not_1_out;
  wire [6:0] keyboard_1_data;
  wire [7:7] not_2_out;

  Keyboard keyboard_1 (.clk(not_1_out), .re(RW), .clr(Reset), .avail(keyboard_1_avail), .data(keyboard_1_data));
  not not_1 (not_1_out, Clk);
  not not_2 (not_2_out[7], keyboard_1_avail);
  assign RDVAL = {{8{1'b0}}, {not_2_out[7], keyboard_1_data}};  // Bit_Extender bit_extender_1
endmodule

module \output  (
  input  [15:0] RSVAL,
  output [6:0] ASCII
);


  assign ASCII = RSVAL[6:0];
endmodule
